// Logisim project guess_the_number_extreme.circ as structural Verilog: 43 circuits, main circuit main
// Contador - S
module main (
  input  Preset,
  input  A3,
  input  A3_2,
  input  A2,
  input  A2_2,
  input  A1,
  input  A1_2,
  input  A0,
  input  A0_2
);

  wire _1DM, _1DS, _1Nor, _1UM, _1US, _2DM, _2DS, _2UM, _2US, _15pontos, A_joga, Acertou, ATZ, B_joga, BTZ,
       chutar, Clear, clock, Clock1, Clock2, Cofin, Cofin2, conf, conf1, conf2, DM, DS, Enable, Igual, Maior,
       Menor, neg1, neg2, parametrosComp, prox, UM, US, X, XfinalN, Y, YfinalN;
  wire [3:0] ADM, ADS, AUM, AUS, BDM, BDS, BUM, BUS, out1, out2, PlacarA, PlacarB, Xfinal, Yfinal;

  Button u_Enable (.out(Enable));
  Button Reset (.out(Clear));
  Button u_UM (.out(_1UM));
  Hex_Digit_Display hex_digit_display_1 (.value(AUM));  // open: dp
  or or_1 (UM, _2UM, _1UM);
  or or_2 (DM, _1DM, _2DM);
  or or_3 (DS, _1DS, _2DS);
  or or_4 (US, _1US, _2US);
  or or_5 (conf, conf1, conf2);
  Clock clock_1 (.out(clock));
  Button u_DS (.out(_1DS));
  Button u_DM (.out(_1DM));
  Hex_Digit_Display hex_digit_display_2 (.value(ADM));  // open: dp
  Hex_Digit_Display hex_digit_display_3 (.value(ADS));  // open: dp
  and and_1 (Clock2, clock, ~A_joga, parametrosComp);  // AND_Gate
  or or_6 (_1Nor, Enable, Clear, _15pontos);
  and and_2 (Clock1, clock, ~B_joga, parametrosComp);  // AND_Gate
  Button u_US (.out(_1US));
  Hex_Digit_Display hex_digit_display_4 (.value(AUS));  // open: dp
  _7_Segment_Display u_7_segment_display_1 (.g(neg1));  // open: f, a, b, e, d, c, dp
  Button Configurar (.out(conf1));
  Hex_Digit_Display hex_digit_display_5 (.value(out1));  // open: dp
  and and_3 (parametrosComp, ~Igual, ~Maior, ~Menor);  // AND_Gate
  LED Configurando (.in(Cofin2));
  LED A_Jogando (.in(A_joga));
  Hex_Digit_Display hex_digit_display_6 (.value(PlacarA));  // open: dp
  _7_Segment_Display u_7_segment_display_2 (.g(XfinalN));  // open: f, a, b, e, d, c, dp
  LED u_Igual (.in(Igual));
  Button u_Chutar (.out(chutar));
  LED u_X (.in(X));
  Hex_Digit_Display hex_digit_display_7 (.value(Xfinal));  // open: dp
  LED u_Maior (.in(Maior));
  // Mostrador2 mostrador2_1: pin names not known; wires that end beside it: Preset, _1Nor, Clear, BUM, UM, BDM, DM, BDS, DS, BUS, US, Cofin, Clock2, conf, BTZ
  Button \Próximo  (.out(prox));
  LED u_Y (.in(Y));
  Hex_Digit_Display hex_digit_display_8 (.value(PlacarB));  // open: dp
  _7_Segment_Display u_7_segment_display_3 (.g(YfinalN));  // open: f, a, b, e, d, c, dp
  LED u_Menor (.in(Menor));
  LED Configurando_2 (.in(Cofin));
  LED B_Jogando (.in(B_joga));
  Hex_Digit_Display hex_digit_display_9 (.value(Yfinal));  // open: dp
  LED u_Acertou (.in(Acertou));
  \Seleção  \seleção_1  (
    .Out1(out1), .In1({A3, A2, A1, A0}), .In2({A3_2, A2_2, A1_2, A0_2}), .Out2(out2), .\Próximo (prox),
    .Iniciar(_1Nor), .Igual(Igual), .Maior(Maior), .Menor(Menor), .Acertou(Acertou), .Chutar(chutar),
    .Negativo___A(neg1), .Negativo___B(neg2), .A_Jogando(A_joga), .B_Jogando(B_joga), .X_final(Xfinal),
    .Y_final(Yfinal), .X_final_negativo(XfinalN), .Y_final_negativo(YfinalN), .X(X), .Y(Y),
    .Placar_A(PlacarA), .Placar_B(PlacarB), .ATZ(ATZ), .BTZ(BTZ), ._15pontos(_15pontos), .Reset(Clear));
  Button UM_2 (.out(_2UM));
  Hex_Digit_Display hex_digit_display_10 (.value(BUM));  // open: dp
  _7_Segment_Display u_7_segment_display_4 (.g(neg2));  // open: f, a, b, e, d, c, dp
  Button DM_2 (.out(_2DM));
  Hex_Digit_Display hex_digit_display_11 (.value(BDS));  // open: dp
  Hex_Digit_Display hex_digit_display_12 (.value(BDM));  // open: dp
  Hex_Digit_Display hex_digit_display_13 (.value(out2));  // open: dp
  Button DS_2 (.out(_2DS));
  Button US_2 (.out(_2US));
  Hex_Digit_Display hex_digit_display_14 (.value(BUS));  // open: dp
  Button Configurar_2 (.out(conf2));
  Mostrador2 mostrador2_2 (
    .Clear(Clear), .Enable(_1Nor), .Preset(Preset), .Configurar(conf), .Clock(Clock1), .DM(UM), .UM(DM),
    .DS(DS), .US(US), .Lamp_Config(Cofin2), .MUM(ADM), .DMM(AUM), .DSS(ADS), .USS(AUS), .Zerou(Clear));

  // Other names for the same wires on the sheet: B0 = A0_2; B1 = A1_2; B2 = A2_2; B3 = A3_2

  // Notes on the sheet:
  //   Controlando Sistema
  //   JoyStick de A
  //   Placar de A
  //   Chutando
  //   Resultado
  //   Placar de B
  //   JoyStick de B
endmodule

module Flip_Flop___D___PC (
  input  Clear,
  input  D,
  input  Clock,
  input  Enable,
  input  Preset,
  output Q,
  output Q_prime
);

  wire and_1_out, and_2_out, and_3_out, and_4_out, not_1_out, not_2_out, not_3_out, not_4_out;

  not not_1 (not_1_out, Clock);
  not not_2 (not_2_out, not_3_out);
  not not_3 (not_3_out, not_1_out);
  and and_1 (and_1_out, not_2_out, Clock);
  not not_4 (not_4_out, D);
  and and_2 (and_2_out, and_1_out, Enable);
  and and_3 (and_3_out, not_4_out, and_2_out);
  and and_4 (and_4_out, and_2_out, D);
  nor nor_1 (Q, Clear, and_3_out, Q_prime);
  nor nor_2 (Q_prime, and_4_out, Q, Preset);
endmodule

module Registrador (
  input  D3,
  input  D2,
  input  D1,
  input  D0,
  input  Clock,
  input  Clear,
  input  Enable,
  input  Preset,
  output [3:0] out_9
);

  Flip_Flop___D___PC ff_d_pc_1 (
    .Clear(Clear), .D(D3), .Clock(Clock), .Enable(Enable), .Preset(Preset), .Q(out_9[3]));  // open: Q_prime
  Flip_Flop___D___PC ff_d_pc_2 (
    .Clear(Clear), .D(D2), .Clock(Clock), .Enable(Enable), .Preset(Preset), .Q(out_9[2]));  // open: Q_prime
  Flip_Flop___D___PC ff_d_pc_3 (
    .Clear(Clear), .D(D1), .Clock(Clock), .Enable(Enable), .Preset(Preset), .Q(out_9[1]));  // open: Q_prime
  Flip_Flop___D___PC ff_d_pc_4 (
    .Clear(Clear), .D(D0), .Clock(Clock), .Enable(Enable), .Preset(Preset), .Q(out_9[0]));  // open: Q_prime
endmodule

module \Condição___Minutos  (
  input  I0,
  input  I1,
  input  I2,
  input  I3,
  output S
);

  wire not_1_out, not_2_out, not_3_out, not_4_out;

  not not_1 (not_1_out, I0);
  not not_2 (not_2_out, I1);
  not not_3 (not_3_out, I2);
  not not_4 (not_4_out, I3);
  and and_1 (S, not_1_out, not_2_out, not_3_out, not_4_out);
endmodule

module Verificador (
  input  [3:0] in_1,
  input  Clock,
  output Q
);

  wire and_1_out, and_2_out, and_3_out, \condição_minutos_1_s , nor_2_out, not_1_out, not_2_out, not_3_out,
       not_4_out;

  not not_1 (not_1_out, Clock);
  not not_2 (not_2_out, not_1_out);
  not not_3 (not_3_out, not_2_out);
  \Condição___Minutos  \condição_minutos_1  (
    .I0(in_1[3]), .I1(in_1[2]), .I2(in_1[1]), .I3(in_1[0]), .S(\condição_minutos_1_s ));
  and and_1 (and_1_out, not_3_out, Clock);
  not not_4 (not_4_out, \condição_minutos_1_s );
  and and_2 (and_2_out, not_4_out, and_1_out);
  and and_3 (and_3_out, and_1_out, \condição_minutos_1_s );
  nor nor_1 (Q, and_2_out, nor_2_out);
  nor nor_2 (nor_2_out, and_3_out, Q);
endmodule

module Latch___RS (
  input  in_1,
  input  in_2,
  output Q,
  output Q_prime
);

  nor nor_1 (Q, in_1, Q_prime);
  nor nor_2 (Q_prime, Q, in_2);
endmodule

module \Botão_Subida  (
  input  \Botão ,
  output Enable
);

  wire not_1_out, not_2_out, not_3_out;

  not not_1 (not_1_out, not_2_out);
  not not_2 (not_2_out, not_3_out);
  not not_3 (not_3_out, Enable);
  D_Flip_Flop d_ff_1 (.clk(\Botão ), .D(not_1_out), .Q(Enable));  // open: Qn, preset, en, reset
endmodule

module \Botão_Descida  (
  input  \Botão ,
  output Enable
);

  wire not_1_out, not_2_out, not_3_out;

  not not_1 (not_1_out, not_3_out);
  not not_2 (not_2_out, Enable);
  not not_3 (not_3_out, not_2_out);
  D_Flip_Flop #(.trigger("falling")) d_ff_1 (.clk(\Botão ), .D(not_1_out), .Q(Enable));  // open: Qn, preset, en, reset
endmodule

module Decodificador (
  input  in_1,
  input  in_2,
  input  in_3,
  input  in_4,
  output [3:0] out_5,
  output [2:0] out_6
);

  wire and_1_out, and_2_out, and_3_out, and_4_out, and_5_out, and_6_out, and_7_out, and_8_out, and_9_out,
       and_10_out, and_11_out, and_12_out, and_13_out, and_14_out, and_15_out, and_16_out, and_17_out,
       and_18_out, and_19_out, and_20_out, and_21_out, and_22_out, and_23_out, and_24_out, and_25_out,
       and_26_out, and_27_out, and_28_out, and_29_out, and_30_out, and_31_out, not_1_out, not_2_out,
       not_3_out, not_4_out, not_5_out, not_6_out, not_7_out, not_8_out, not_9_out, not_10_out, not_11_out,
       not_12_out, not_13_out, not_14_out, not_15_out, not_16_out, not_17_out, not_18_out, not_19_out,
       not_20_out, not_21_out, not_22_out, not_23_out, not_24_out, not_25_out, not_26_out, not_27_out,
       not_28_out, not_29_out, not_30_out, not_31_out, not_32_out, not_33_out, not_34_out, not_35_out,
       not_36_out, not_37_out, not_38_out, not_39_out, not_40_out, not_41_out, not_42_out, not_43_out,
       not_44_out, not_45_out, or_5_out, xor_1_out;

  not not_1 (not_1_out, in_4);
  not not_2 (not_2_out, in_3);
  not not_3 (not_3_out, in_2);
  not not_4 (not_4_out, in_1);
  not not_5 (not_5_out, in_4);
  not not_6 (not_6_out, in_3);
  not not_7 (not_7_out, in_3);
  not not_8 (not_8_out, in_4);
  not not_9 (not_9_out, in_2);
  not not_10 (not_10_out, in_1);
  not not_11 (not_11_out, in_4);
  not not_12 (not_12_out, in_2);
  not not_13 (not_13_out, in_3);
  not not_14 (not_14_out, in_1);
  not not_15 (not_15_out, in_1);
  not not_16 (not_16_out, in_4);
  not not_17 (not_17_out, in_3);
  not not_18 (not_18_out, in_2);
  not not_19 (not_19_out, in_1);
  not not_20 (not_20_out, in_2);
  not not_21 (not_21_out, in_2);
  not not_22 (not_22_out, in_1);
  not not_23 (not_23_out, in_4);
  not not_24 (not_24_out, in_1);
  and and_1 (and_1_out, in_3, in_1);
  and and_2 (and_2_out, not_1_out, not_2_out, not_3_out, not_4_out);
  and and_3 (and_3_out, not_5_out, not_6_out);
  and and_4 (and_4_out, in_4, not_7_out);
  and and_5 (and_5_out, not_8_out, in_3, not_9_out, not_10_out);
  and and_6 (and_6_out, not_11_out, in_3, in_2, in_1);
  and and_7 (and_7_out, in_4, in_3, not_12_out, in_1);
  not not_25 (not_25_out, in_4);
  not not_26 (not_26_out, in_3);
  not not_27 (not_27_out, in_2);
  not not_28 (not_28_out, in_1);
  not not_29 (not_29_out, in_2);
  not not_30 (not_30_out, in_2);
  not not_31 (not_31_out, in_3);
  not not_32 (not_32_out, in_1);
  not not_33 (not_33_out, in_4);
  not not_34 (not_34_out, in_1);
  not not_35 (not_35_out, in_4);
  not not_36 (not_36_out, in_3);
  and and_8 (and_8_out, in_4, not_13_out, not_14_out);
  and and_9 (and_9_out, in_4, in_3);
  and and_10 (and_10_out, in_2, not_15_out);
  and and_11 (and_11_out, in_4, in_2);
  and and_12 (and_12_out, not_16_out, not_17_out, not_18_out, not_19_out);
  and and_13 (and_13_out, in_3, not_20_out);
  and and_14 (and_14_out, not_21_out, not_22_out);
  and and_15 (and_15_out, not_23_out, in_3, in_2, not_24_out);
  and and_16 (and_16_out, not_25_out, not_26_out, not_27_out, not_28_out);
  and and_17 (and_17_out, in_4, not_29_out);
  and and_18 (and_18_out, in_3, not_30_out, in_1);
  and and_19 (and_19_out, in_4, not_31_out, in_1);
  and and_20 (and_20_out, in_3, in_2, not_32_out);
  and and_21 (and_21_out, not_33_out, in_2, not_34_out);
  and and_22 (and_22_out, not_35_out, not_36_out, in_2);
  or or_1 (out_6[2], and_8_out, and_9_out, and_10_out, and_11_out, and_12_out);
  or or_2 (out_5[2], in_4, and_13_out, and_14_out, and_15_out);
  or or_3 (out_5[1], in_4, in_2, and_1_out, and_2_out);
  or or_4 (out_5[0], and_3_out, and_4_out, and_5_out, and_6_out, and_7_out);
  or or_5 (or_5_out, and_16_out, and_17_out, and_18_out, and_19_out, and_20_out);
  not not_37 (not_37_out, in_3);
  not not_38 (not_38_out, in_1);
  not not_39 (not_39_out, in_4);
  xor xor_1 (xor_1_out, in_3, in_2);
  not not_40 (not_40_out, in_4);
  not not_41 (not_41_out, in_2);
  not not_42 (not_42_out, in_4);
  not not_43 (not_43_out, in_4);
  not not_44 (not_44_out, in_2);
  not not_45 (not_45_out, in_3);
  or or_6 (out_6[1], or_5_out, and_22_out, and_21_out);
  and and_23 (and_23_out, in_4, not_37_out);
  and and_24 (and_24_out, in_2, not_38_out);
  and and_25 (and_25_out, in_4, in_2);
  and and_26 (and_26_out, not_39_out, xor_1_out);
  and and_27 (and_27_out, not_40_out, not_41_out);
  and and_28 (and_28_out, not_42_out, in_1);
  and and_29 (and_29_out, not_43_out, in_3, in_2);
  and and_30 (and_30_out, not_44_out, in_1);
  and and_31 (and_31_out, in_4, not_45_out);
  or or_7 (out_5[3], and_23_out, and_24_out, and_25_out, and_26_out);
  or or_8 (out_6[0], and_27_out, and_28_out, and_29_out, and_30_out, and_31_out);
  _7_Segment_Display u_7_segment_display_1 (
    .g(out_5[3]), .f(out_5[2]), .a(out_5[1]), .b(out_5[0]), .e(out_6[2]), .d(out_6[1]), .c(out_6[0]));  // open: dp
endmodule

module Comparador (
  input  [3:0] \N_mág ,
  input  [3:0] Chute,
  input  Ctrl,
  output I0___I1,
  output Maior,
  output Menor
);

  wire A0___B0_out, A1___B1_2_out, A1___B1_3_out, A1___B1_out, nor_1_out, not_1_out, not_2_out, not_3_out,
       not_4_out, or_1_out, xnor_1_out, xnor_2_out, xnor_3_out, xnor_4_out;

  xnor xnor_1 (xnor_1_out, Chute[0], \N_mág [0]);
  xnor xnor_2 (xnor_2_out, Chute[1], \N_mág [1]);
  xnor xnor_3 (xnor_3_out, Chute[2], \N_mág [2]);
  xnor xnor_4 (xnor_4_out, Chute[3], \N_mág [3]);
  not not_1 (not_1_out, \N_mág [0]);
  not not_2 (not_2_out, \N_mág [1]);
  not not_3 (not_3_out, \N_mág [2]);
  not not_4 (not_4_out, \N_mág [3]);
  and A0___B0 (A0___B0_out, Chute[0], not_1_out);
  and A1___B1 (A1___B1_out, Chute[1], not_2_out);
  and A1___B1_2 (A1___B1_2_out, Chute[2], not_3_out);
  and A1___B1_3 (A1___B1_3_out, xnor_1_out, xnor_2_out, xnor_3_out, Chute[3], not_4_out);
  and and_1 (I0___I1, xnor_4_out, xnor_3_out, xnor_2_out, xnor_1_out, Ctrl);
  or or_1 (or_1_out, A0___B0_out, A1___B1_out, A1___B1_2_out, A1___B1_3_out);
  and and_2 (Maior, or_1_out, Ctrl);
  nor nor_1 (nor_1_out, Maior, I0___I1);
  and and_3 (Menor, nor_1_out, Ctrl);
endmodule

module Multiplexador___4_in (
  input  [3:0] E1,
  input  [3:0] E2,
  input  M,
  output [3:0] out_4
);

  wire and_1_out, and_2_out, and_3_out, and_4_out, and_5_out, and_6_out, and_7_out, and_8_out, not_1_out,
       not_2_out, not_3_out, not_4_out;

  not not_1 (not_1_out, M);
  not not_2 (not_2_out, M);
  not not_3 (not_3_out, M);
  not not_4 (not_4_out, M);
  and and_1 (and_1_out, E1[0], not_1_out);
  and and_2 (and_2_out, E2[0], M);
  and and_3 (and_3_out, E1[1], not_2_out);
  and and_4 (and_4_out, E2[1], M);
  and and_5 (and_5_out, E1[2], not_3_out);
  and and_6 (and_6_out, E2[2], M);
  and and_7 (and_7_out, E1[3], not_4_out);
  and and_8 (and_8_out, E2[3], M);
  or or_1 (out_4[0], and_1_out, and_2_out);
  or or_2 (out_4[1], and_3_out, and_4_out);
  or or_3 (out_4[2], and_5_out, and_6_out);
  or or_4 (out_4[3], and_7_out, and_8_out);
endmodule

module Display_Jogador (
  input  [3:0] in_1,
  output [3:0] out_2,
  output [2:0] out_3
);

  Decodificador decodificador_1 (
    .in_1(in_1[0]), .in_2(in_1[1]), .in_3(in_1[2]), .in_4(in_1[3]), .out_5(out_2), .out_6(out_3));
endmodule

module Registrador_FFP (
  input  D3,
  input  D2,
  input  D1,
  input  D0,
  input  Clock,
  input  Clear,
  input  Enable,
  input  Preset,
  output [3:0] out_9
);

  D_Flip_Flop d_ff_1 (.clk(Clock), .D(D3), .Q(out_9[3]), .preset(Preset), .en(Enable), .reset(Clear));  // open: Qn
  D_Flip_Flop d_ff_2 (.clk(Clock), .D(D2), .Q(out_9[2]), .preset(Preset), .en(Enable), .reset(Clear));  // open: Qn
  D_Flip_Flop d_ff_3 (.clk(Clock), .D(D1), .Q(out_9[1]), .preset(Preset), .en(Enable), .reset(Clear));  // open: Qn
  D_Flip_Flop d_ff_4 (.clk(Clock), .D(D0), .Q(out_9[0]), .preset(Preset), .en(Enable), .reset(Clear));  // open: Qn
endmodule

module Contador_S (
  input  US,
  input  Configurar,
  input  Clock,
  input  Preset,
  input  Enable,
  input  Clear,
  output [3:0] Visor,
  output \Clock___Próx 
);

  wire and_1_out, multiplexador_1_in_1_out_4, not_1_out, or_1_out, subtrator_s_1_cp;
  wire [3:0] registrador_ffp_1_out_9;

  not not_1 (not_1_out, Configurar);
  and and_1 (and_1_out, not_1_out, Clock);
  Multiplexador___1_in multiplexador_1_in_1 (
    .out_4(multiplexador_1_in_1_out_4), .E0(and_1_out), .E1(US), .M(Configurar));
  Hex_Digit_Display hex_digit_display_1 (.value(Visor));  // open: dp
  Registrador_FFP registrador_ffp_1 (
    .D3(Visor[3]), .D2(Visor[2]), .D1(Visor[1]), .D0(Visor[0]), .Clock(multiplexador_1_in_1_out_4),
    .Clear(Clear), .Enable(or_1_out), .Preset(Preset), .out_9(registrador_ffp_1_out_9));
  or or_1 (or_1_out, Configurar, Enable);
  Subtrator_S subtrator_s_1 (
    .in_1(registrador_ffp_1_out_9), .D0(Visor[3]), .D1(Visor[2]), .D2(Visor[1]), .D3(Visor[0]),
    .CP(subtrator_s_1_cp));
  and and_2 (\Clock___Próx , subtrator_s_1_cp, not_1_out);
endmodule

module Contador_DS (
  input  US,
  input  Configurar,
  input  Clock,
  input  Preset,
  input  Clear,
  input  Enable,
  output [3:0] Visor,
  output \Clock___Próx 
);

  wire and_1_out, multiplexador_1_in_1_out_4, not_1_out, or_1_out, subtrator_ds_1_cp;
  wire [3:0] registrador_ffp_1_out_9;

  not not_1 (not_1_out, Configurar);
  and and_1 (and_1_out, not_1_out, Clock);
  Multiplexador___1_in multiplexador_1_in_1 (
    .out_4(multiplexador_1_in_1_out_4), .E0(and_1_out), .E1(US), .M(Configurar));
  Registrador_FFP registrador_ffp_1 (
    .D3(Visor[3]), .D2(Visor[2]), .D1(Visor[1]), .D0(Visor[0]), .Clock(multiplexador_1_in_1_out_4),
    .Clear(Clear), .Enable(or_1_out), .Preset(Preset), .out_9(registrador_ffp_1_out_9));
  or or_1 (or_1_out, Configurar, Enable);
  Subtrator_DS subtrator_ds_1 (
    .in_1(registrador_ffp_1_out_9), .D0(Visor[3]), .D1(Visor[2]), .D2(Visor[1]), .D3(Visor[0]),
    .CP(subtrator_ds_1_cp));
  Hex_Digit_Display hex_digit_display_1 (.value(Visor));  // open: dp
  and and_2 (\Clock___Próx , subtrator_ds_1_cp, not_1_out);
endmodule

module Contador_SS (
  input  US,
  input  Configurar,
  input  Clock,
  input  Preset,
  input  Enable,
  input  Clear,
  output [3:0] Visor,
  output \Clock___Próx 
);

  wire and_1_out, and_2_out, not_1_out, or_1_out, or_2_out, subtrator_s_1_cp, verificador_ffp_1_q;
  wire [3:0] registrador_ffp_1_out_9;

  not not_1 (not_1_out, Configurar);
  and and_1 (and_1_out, US, Configurar);
  and and_2 (and_2_out, not_1_out, Clock);
  or or_1 (or_1_out, and_1_out, and_2_out);
  Hex_Digit_Display hex_digit_display_1 (.value(Visor));  // open: dp
  Registrador_FFP registrador_ffp_1 (
    .D3(Visor[3]), .D2(Visor[2]), .D1(Visor[1]), .D0(Visor[0]), .Clock(or_1_out), .Clear(Clear),
    .Enable(or_2_out), .Preset(Preset), .out_9(registrador_ffp_1_out_9));
  or or_2 (or_2_out, Configurar, Enable);
  Subtrator_S subtrator_s_1 (
    .in_1(registrador_ffp_1_out_9), .D0(Visor[3]), .D1(Visor[2]), .D2(Visor[1]), .D3(Visor[0]),
    .CP(subtrator_s_1_cp));
  Verificador_FFP verificador_ffp_1 (.Entrada(Visor), .Clock(Clock), .Q(verificador_ffp_1_q));
  and and_3 (\Clock___Próx , subtrator_s_1_cp, not_1_out, verificador_ffp_1_q);
endmodule

module Contador_DSS (
  input  US,
  input  Configurar,
  input  Clock,
  input  Preset,
  input  Enable,
  input  Clear,
  output [3:0] Visor,
  output \Clock___Próx 
);

  wire and_1_out, and_2_out, not_1_out, or_1_out, or_2_out, subtrator_ds_1_cp, verificador_ffp_1_q;
  wire [3:0] registrador_ffp_1_out_9;

  not not_1 (not_1_out, Configurar);
  and and_1 (and_1_out, US, Configurar);
  or or_1 (or_1_out, and_1_out, and_2_out);
  and and_2 (and_2_out, not_1_out, Clock);
  Hex_Digit_Display hex_digit_display_1 (.value(Visor));  // open: dp
  Registrador_FFP registrador_ffp_1 (
    .D3(Visor[3]), .D2(Visor[2]), .D1(Visor[1]), .D0(Visor[0]), .Clock(or_1_out), .Clear(Clear),
    .Enable(or_2_out), .Preset(Preset), .out_9(registrador_ffp_1_out_9));
  or or_2 (or_2_out, Configurar, Enable);
  Subtrator_DS subtrator_ds_1 (
    .in_1(registrador_ffp_1_out_9), .D0(Visor[3]), .D1(Visor[2]), .D2(Visor[1]), .D3(Visor[0]),
    .CP(subtrator_ds_1_cp));
  Verificador_FFP verificador_ffp_1 (.Entrada(Visor), .Clock(Clock), .Q(verificador_ffp_1_q));
  and and_3 (\Clock___Próx , subtrator_ds_1_cp, verificador_ffp_1_q);
endmodule

module Mostrador (
  input  DM,
  input  UM,
  input  DS,
  input  US,
  input  Clock,
  input  Preset,
  input  Clear,
  input  Configurar,
  input  Enable,
  output [3:0] DM_2,
  output [3:0] M,
  output [3:0] DS_2,
  output [3:0] S,
  output Lamp_Config,
  output TZ
);

  wire and_1_out, and_2_out, and_3_out, and_4_out, and_5_out, and_6_out, \botão_subida_2_enable ,
       \botão_subida_4_enable , \contador_ds_1_clock___próx , \contador_ds_2_clock___próx ,
       \contador_s_1_clock___próx , \contador_s_2_clock___próx , not_1_out, not_2_out, not_3_out, not_4_out,
       or_1_out, verificador_1_q, verificador_2_q;

  and and_1 (and_1_out, \contador_s_2_clock___próx , and_4_out, and_3_out, \contador_ds_1_clock___próx );
  Hex_Digit_Display hex_digit_display_1 (.value(DM_2));  // open: dp
  Contador_DS contador_ds_1 (
    .Visor(DM_2), .US(DM), .Configurar(and_2_out), .Clock(and_3_out), .Clear(Clear),
    .Enable(\botão_subida_2_enable ), .Preset(Preset), .\Clock___Próx (\contador_ds_1_clock___próx ));
  and and_2 (and_2_out, not_1_out, \botão_subida_4_enable );
  not not_1 (not_1_out, \botão_subida_2_enable );
  Verificador verificador_1 (.Clock(Clock), .Q(verificador_1_q), .in_1(M));
  and and_3 (and_3_out, verificador_1_q, and_4_out, \contador_s_1_clock___próx );
  Hex_Digit_Display hex_digit_display_2 (.value(M));  // open: dp
  Contador_S contador_s_1 (
    .Visor(M), .\Clock___Próx (\contador_s_1_clock___próx ), .Preset(Preset),
    .Enable(\botão_subida_2_enable ), .Clear(Clear), .Clock(and_4_out), .Configurar(and_5_out), .US(UM));
  not not_2 (not_2_out, \botão_subida_2_enable );
  Verificador verificador_2 (.Clock(Clock), .Q(verificador_2_q), .in_1(DS_2));
  and and_4 (and_4_out, verificador_2_q, \contador_s_2_clock___próx , \contador_ds_2_clock___próx );
  and and_5 (and_5_out, not_2_out, \botão_subida_4_enable );
  Hex_Digit_Display hex_digit_display_3 (.value(DS_2));  // open: dp
  Contador_DS contador_ds_2 (
    .Visor(DS_2), .US(DS), .Configurar(and_6_out), .Clock(\contador_s_2_clock___próx ), .Clear(Clear),
    .Enable(\botão_subida_2_enable ), .Preset(Preset), .\Clock___Próx (\contador_ds_2_clock___próx ));
  and and_6 (and_6_out, not_3_out, \botão_subida_4_enable );
  not not_3 (not_3_out, \botão_subida_2_enable );
  \Botão_Subida  \botão_subida_1  (.\Botão (and_1_out), .Enable(TZ));
  Contador_S contador_s_2 (
    .Visor(S), .\Clock___Próx (\contador_s_2_clock___próx ), .Preset(Preset),
    .Enable(\botão_subida_2_enable ), .Clear(Clear), .Clock(Clock), .Configurar(Lamp_Config), .US(US));
  Hex_Digit_Display hex_digit_display_4 (.value(S));  // open: dp
  \Botão_Subida  \botão_subida_2  (.\Botão (or_1_out), .Enable(\botão_subida_2_enable ));
  or or_1 (or_1_out, and_1_out, Enable);
  \Botão_Subida  \botão_subida_3  ();  // open: Botão, Enable
  and and_7 (Lamp_Config, not_4_out, \botão_subida_4_enable );
  not not_4 (not_4_out, \botão_subida_2_enable );
  \Botão_Subida  \botão_subida_4  (.\Botão (Configurar), .Enable(\botão_subida_4_enable ));
endmodule

module Mostrador2 (
  input  Configurar,
  input  DM,
  input  UM,
  input  DS,
  input  US,
  input  Clock,
  input  Clear,
  input  Enable,
  input  Preset,
  output Lamp_Config,
  output [3:0] DMM,
  output [3:0] MUM,
  output [3:0] DSS,
  output [3:0] USS,
  output Zerou
);

  wire and_4_out, \botão_subida_1_enable , \botão_subida_2_enable , \contador_dss_2_clock___próx ,
       \contador_ss_1_clock___próx , \contador_ss_2_clock___próx , or_2_out, Z;
  wire [3:0] and_2_out;

  or or_1 (Zerou, Z, Clear);
  and and_1 (Z, and_2_out[0], and_2_out[1], and_2_out[2], and_2_out[3]);
  or or_2 (or_2_out, Z, Enable);
  \Botão_Subida  \botão_subida_1  (.\Botão (or_2_out), .Enable(\botão_subida_1_enable ));
  assign and_2_out = ~USS & ~DSS & ~MUM & ~DMM;  // AND_Gate and_2, 4 bits wide
  Hex_Digit_Display hex_digit_display_1 (.value(DMM));  // open: dp
  Contador_DSS contador_dss_1 (
    .Visor(DMM), .US(DM), .Configurar(Lamp_Config), .Clock(\contador_ss_1_clock___próx ), .Preset(Preset),
    .Enable(\botão_subida_1_enable ), .Clear(Clear));  // open: Clock___Próx
  Hex_Digit_Display hex_digit_display_2 (.value(MUM));  // open: dp
  Contador_SS contador_ss_1 (
    .US(UM), .Configurar(Lamp_Config), .Clock(\contador_dss_2_clock___próx ), .Visor(MUM), .Preset(Preset),
    .Enable(\botão_subida_1_enable ), .Clear(Clear), .\Clock___Próx (\contador_ss_1_clock___próx ));
  Hex_Digit_Display hex_digit_display_3 (.value(DSS));  // open: dp
  Contador_DSS contador_dss_2 (
    .Visor(DSS), .US(DS), .Configurar(Lamp_Config), .\Clock___Próx (\contador_dss_2_clock___próx ),
    .Clock(\contador_ss_2_clock___próx ), .Preset(Preset), .Enable(\botão_subida_1_enable ), .Clear(Clear));
  Hex_Digit_Display hex_digit_display_4 (.value(USS));  // open: dp
  Contador_SS contador_ss_2 (
    .US(US), .Configurar(Lamp_Config), .Clock(and_4_out), .Visor(USS), .Preset(Preset),
    .Enable(\botão_subida_1_enable ), .Clear(Clear), .\Clock___Próx (\contador_ss_2_clock___próx ));
  and and_3 (Lamp_Config, \botão_subida_2_enable , ~\botão_subida_1_enable );  // AND_Gate
  and and_4 (and_4_out, Clock, ~Z);  // AND_Gate
  \Botão_Subida  \botão_subida_2  (.\Botão (Configurar), .Enable(\botão_subida_2_enable ));
endmodule

module Multiplexador___1_in (
  input  E0,
  input  E1,
  input  M,
  output out_4
);

  wire and_1_out, and_2_out, and_3_out, not_1_out;

  not not_1 (not_1_out, M);
  and and_1 (and_1_out, E0, not_1_out);
  and and_2 (and_2_out, E1, M);
  and and_3 (and_3_out, E0, E1);
  or or_1 (out_4, and_1_out, and_2_out, and_3_out);
endmodule

module Subtrator_S (
  input  [3:0] in_1,
  output D0,
  output D1,
  output D2,
  output D3,
  output CP
);

  wire and_1_out, and_2_out, and_3_out, and_4_out, and_5_out, and_6_out, and_7_out, and_8_out, not_1_out,
       not_2_out, not_3_out, not_4_out, not_5_out, not_6_out, not_7_out, not_8_out, not_9_out, not_10_out,
       not_11_out, not_12_out, not_14_out, not_15_out, not_16_out, not_17_out;

  not not_1 (not_1_out, in_1[3]);
  not not_2 (not_2_out, in_1[2]);
  not not_3 (not_3_out, in_1[1]);
  not not_4 (not_4_out, in_1[0]);
  not not_5 (not_5_out, in_1[2]);
  not not_6 (not_6_out, in_1[3]);
  not not_7 (not_7_out, in_1[3]);
  not not_8 (not_8_out, in_1[0]);
  not not_9 (not_9_out, in_1[3]);
  not not_10 (not_10_out, in_1[1]);
  not not_11 (not_11_out, in_1[0]);
  not not_12 (not_12_out, in_1[0]);
  not not_13 (D3, in_1[0]);
  not not_14 (not_14_out, in_1[3]);
  not not_15 (not_15_out, in_1[2]);
  not not_16 (not_16_out, in_1[1]);
  not not_17 (not_17_out, in_1[0]);
  and and_1 (and_1_out, not_1_out, not_2_out, not_3_out, not_4_out);
  and and_2 (and_2_out, in_1[3], not_5_out, in_1[0]);
  and and_3 (and_3_out, not_6_out, in_1[2], in_1[0]);
  and and_4 (and_4_out, not_7_out, in_1[2], in_1[1]);
  and and_5 (and_5_out, in_1[3], not_8_out);
  and and_6 (and_6_out, not_9_out, in_1[1], in_1[0]);
  and and_7 (and_7_out, in_1[2], not_10_out, not_11_out);
  and and_8 (and_8_out, in_1[3], not_12_out);
  and and_9 (CP, not_14_out, not_15_out, not_16_out, not_17_out);
  or or_1 (D0, and_1_out, and_2_out);
  or or_2 (D1, and_3_out, and_4_out, and_5_out);
  or or_3 (D2, and_6_out, and_7_out, and_8_out);
endmodule

module Subtrator_DS (
  input  [3:0] in_1,
  output D0,
  output D1,
  output D2,
  output D3,
  output CP
);

  wire and_2_out, and_3_out, and_4_out, and_5_out, and_6_out, and_7_out, not_1_out, not_2_out, not_3_out,
       not_4_out, not_5_out, not_6_out, not_7_out, not_8_out, not_9_out, not_10_out, not_12_out, not_13_out,
       not_14_out, not_15_out;

  not not_1 (not_1_out, in_1[2]);
  not not_2 (not_2_out, in_1[2]);
  not not_3 (not_3_out, in_1[1]);
  not not_4 (not_4_out, in_1[0]);
  not not_5 (not_5_out, in_1[3]);
  not not_6 (not_6_out, in_1[3]);
  not not_7 (not_7_out, in_1[3]);
  not not_8 (not_8_out, in_1[1]);
  not not_9 (not_9_out, in_1[0]);
  not not_10 (not_10_out, in_1[0]);
  not not_11 (D3, in_1[0]);
  not not_12 (not_12_out, in_1[3]);
  not not_13 (not_13_out, in_1[2]);
  not not_14 (not_14_out, in_1[1]);
  not not_15 (not_15_out, in_1[0]);
  and and_1 (D0, in_1[3], not_1_out, in_1[0]);
  and and_2 (and_2_out, not_2_out, not_3_out, not_4_out);
  and and_3 (and_3_out, not_5_out, in_1[2], in_1[0]);
  and and_4 (and_4_out, not_6_out, in_1[2], in_1[1]);
  and and_5 (and_5_out, not_7_out, in_1[1], in_1[0]);
  and and_6 (and_6_out, in_1[2], not_8_out, not_9_out);
  and and_7 (and_7_out, in_1[3], not_10_out);
  and and_8 (CP, not_12_out, not_13_out, not_14_out, not_15_out);
  or or_1 (D1, and_2_out, and_3_out, and_4_out);
  or or_2 (D2, and_5_out, and_6_out, and_7_out);
endmodule

module \Cronômetro  (
  input  Preset,
  input  Enable,
  input  Clear
);

  wire DM_out, mostrador_1_p9, mostrador_1_p11, mostrador_1_p12, mostrador_1_p13, mostrador_1_p14, UM_out;
  wire [3:0] mostrador_1_p4, mostrador_1_p7, mostrador_1_p8, mostrador_1_p10;

  Button UM (.out(UM_out));
  Button DM (.out(DM_out));
  Hex_Digit_Display hex_digit_display_1 (.value(mostrador_1_p4));  // open: dp
  // Mostrador mostrador_1: pin names not known; wires that end beside it: Preset, Enable, Clear, mostrador_1_p4, DM_out, UM_out, mostrador_1_p7, mostrador_1_p8, mostrador_1_p9, mostrador_1_p10, mostrador_1_p11, mostrador_1_p12, mostrador_1_p13, mostrador_1_p14
  Hex_Digit_Display hex_digit_display_2 (.value(mostrador_1_p7));  // open: dp
  Hex_Digit_Display hex_digit_display_3 (.value(mostrador_1_p8));  // open: dp
  Hex_Digit_Display hex_digit_display_4 (.value(mostrador_1_p10));  // open: dp
  Button DS (.out(mostrador_1_p9));
  Button US (.out(mostrador_1_p11));
  LED Configurando (.in(mostrador_1_p12));
  Button Configurar (.out(mostrador_1_p14));
  Clock clock_1 (.out(mostrador_1_p13));
endmodule

module Chutar (
  input  in_1,
  input  in_2,
  input  in_3,
  input  in_4,
  output Negativo
);

  wire [3:0] \converte_1_saída ;

  Converte converte_1 (.A3(in_1), .A2(in_2), .A1(in_3), .A0(in_4), .\Saída (\converte_1_saída ), .Negativo(Negativo));
  Hex_Digit_Display hex_digit_display_1 (.value(\converte_1_saída ));  // open: dp
  Hex_Digit_Display hex_digit_display_2 ();  // open: value, dp
endmodule

module Converte (
  input  A3,
  input  A2,
  input  A1,
  input  A0,
  output [3:0] \Saída ,
  output Negativo
);

  wire and_2_out, and_3_out, and_4_out, and_5_out, and_6_out, and_7_out, and_8_out, not_1_out, not_2_out,
       not_3_out, not_4_out, not_5_out, not_6_out, not_7_out, not_8_out, not_9_out, not_10_out, not_11_out;

  not not_1 (not_1_out, A2);
  not not_2 (not_2_out, A1);
  not not_3 (not_3_out, A0);
  not not_4 (not_4_out, A3);
  not not_5 (not_5_out, A1);
  not not_6 (not_6_out, A0);
  not not_7 (not_7_out, A2);
  not not_8 (not_8_out, A2);
  not not_9 (not_9_out, A3);
  not not_10 (not_10_out, A0);
  not not_11 (not_11_out, A1);
  and and_1 (\Saída [3], A3, not_1_out, not_2_out, not_3_out);
  and and_2 (and_2_out, not_4_out, A2);
  and and_3 (and_3_out, A2, not_5_out, not_6_out);
  and and_4 (and_4_out, A3, not_7_out, A0);
  and and_5 (and_5_out, A3, not_8_out, A1);
  and and_6 (and_6_out, not_9_out, A1);
  and and_7 (and_7_out, A1, not_10_out);
  and and_8 (and_8_out, A3, not_11_out, A0);
  or or_1 (\Saída [2], and_2_out, and_3_out, and_4_out, and_5_out);
  or or_2 (\Saída [1], and_6_out, and_7_out, and_8_out);

  assign Negativo = A3;
  assign \Saída [0] = A0;
endmodule

module Somador__7_8 (
  input  [3:0] in_1,
  input  [3:0] in_2,
  output sinal,
  output [3:0] out_4
);

  wire and_1_out, and_2_out, and_3_out, and_4_out, and_5_out, and_6_out, and_7_out, and_8_out, and_9_out,
       and_10_out, and_11_out, and_12_out, and_13_out, and_14_out, and_15_out, and_16_out, and_17_out,
       and_18_out, and_19_out, and_20_out, and_21_out, and_22_out, and_23_out, and_24_out, and_25_out,
       and_26_out, and_27_out, and_28_out, and_29_out, and_30_out, and_31_out, and_32_out, and_33_out,
       and_34_out, and_35_out, and_36_out, and_37_out, and_38_out, and_39_out, and_40_out, and_41_out,
       and_42_out, and_43_out, and_44_out, and_45_out, and_46_out, and_47_out, and_48_out, and_49_out,
       and_50_out, and_51_out, and_52_out, and_53_out, and_54_out, and_55_out, and_56_out, and_57_out,
       and_58_out, and_59_out, and_60_out, and_61_out, and_62_out, and_63_out, and_64_out, and_65_out,
       and_66_out, and_67_out, and_68_out, and_69_out, and_70_out, and_71_out, and_72_out, and_73_out,
       and_74_out, and_75_out, and_76_out, and_77_out, and_78_out, and_79_out, and_80_out, and_81_out,
       and_82_out, and_83_out, and_84_out, and_85_out, and_86_out, and_87_out, and_88_out, and_89_out,
       and_90_out, and_91_out, and_92_out, and_93_out, and_94_out, and_95_out, and_96_out, and_97_out,
       and_98_out, and_99_out, and_100_out, and_101_out, and_102_out, and_103_out, and_104_out, and_105_out,
       and_106_out, and_107_out, and_108_out, and_109_out, and_110_out, and_111_out, and_112_out,
       and_113_out, and_114_out, and_115_out, and_116_out, and_117_out, and_118_out, not_1_out, not_2_out,
       not_3_out, not_4_out, not_5_out, not_6_out, not_7_out, not_8_out, not_9_out, not_10_out, not_11_out,
       not_12_out, not_13_out, not_14_out, not_15_out, not_16_out, not_17_out, not_18_out, not_19_out,
       not_20_out, not_21_out, not_22_out, not_23_out, not_24_out, not_25_out, not_26_out, not_27_out,
       not_28_out, not_29_out, not_30_out, not_31_out, not_32_out, not_33_out, not_34_out, not_35_out,
       not_36_out, not_37_out, not_38_out, not_39_out, not_40_out, not_41_out, not_42_out, not_43_out,
       not_44_out, not_45_out, not_46_out, not_47_out, not_48_out, not_49_out, not_50_out, not_51_out,
       not_52_out, not_53_out, not_54_out, not_55_out, not_56_out, not_57_out, not_58_out, not_59_out,
       not_60_out, not_61_out, not_62_out, not_63_out, not_64_out, not_65_out, not_66_out, not_67_out,
       not_68_out, not_69_out, not_70_out, not_71_out, not_72_out, not_73_out, not_74_out, not_75_out,
       not_76_out, not_77_out, not_78_out, not_79_out, not_80_out, not_81_out, not_82_out, not_83_out,
       not_84_out, not_85_out, not_86_out, not_87_out, not_88_out, not_89_out, not_90_out, not_91_out,
       not_92_out, not_93_out, not_94_out, not_95_out, not_96_out, not_97_out, not_98_out, not_99_out,
       not_100_out, not_101_out, not_102_out, not_103_out, not_104_out, not_105_out, not_106_out,
       not_107_out, not_108_out, not_109_out, not_110_out, not_111_out, not_112_out, not_113_out,
       not_114_out, not_115_out, not_116_out, not_117_out, not_118_out, not_119_out, not_120_out,
       not_121_out, not_122_out, not_123_out, not_124_out, not_125_out, not_126_out, not_127_out,
       not_128_out, not_129_out, not_130_out, not_131_out, not_132_out, not_133_out, not_134_out,
       not_135_out, not_136_out, not_137_out, not_138_out, not_139_out, not_140_out, not_141_out,
       not_142_out, not_143_out, not_144_out, not_145_out, not_146_out, not_147_out, not_148_out,
       not_149_out, not_150_out, not_151_out, not_152_out, not_153_out, not_154_out, not_155_out,
       not_156_out, not_157_out, not_158_out, not_159_out, not_160_out, not_161_out, not_162_out,
       not_163_out, not_164_out, not_165_out, not_166_out, not_167_out, not_168_out, not_169_out,
       not_170_out, not_171_out, not_172_out, not_173_out, not_174_out, not_175_out, not_176_out,
       not_177_out, not_178_out, not_179_out, not_180_out, not_181_out, not_182_out, not_183_out,
       not_184_out, not_185_out, not_186_out, not_187_out, not_188_out, not_189_out, not_190_out,
       not_191_out, not_192_out, not_193_out, not_194_out, not_195_out, not_196_out, not_197_out,
       not_198_out, not_199_out, not_200_out, not_201_out, not_202_out, not_203_out, not_204_out,
       not_205_out, not_206_out, not_207_out, not_208_out, not_209_out, not_210_out, not_211_out,
       not_212_out, not_213_out, not_214_out, not_215_out, not_216_out, not_217_out, not_218_out,
       not_219_out, not_220_out, not_221_out, not_222_out, not_223_out, not_224_out, not_225_out,
       not_226_out, not_227_out, not_228_out, not_229_out, not_230_out, not_231_out, not_232_out,
       not_233_out, not_234_out, not_235_out, not_236_out, not_237_out, not_238_out, not_239_out,
       not_240_out, not_241_out, not_242_out, not_243_out, not_244_out, not_245_out, not_246_out,
       not_247_out, not_248_out, not_249_out, not_250_out, not_251_out, not_252_out, not_253_out,
       not_254_out, not_255_out, not_256_out, not_257_out, not_258_out, not_259_out, not_260_out,
       not_261_out, not_262_out, not_263_out, not_264_out, not_265_out, not_266_out, not_267_out,
       not_268_out, not_269_out, not_270_out, not_271_out, not_272_out, not_273_out, not_274_out,
       not_275_out, not_276_out, not_277_out, not_278_out, not_279_out, not_280_out, not_281_out,
       not_282_out, not_283_out, not_284_out, not_285_out, not_286_out, not_287_out, not_288_out,
       not_289_out, not_290_out, not_291_out, not_292_out, not_293_out, not_294_out, not_295_out,
       not_296_out, not_297_out, not_298_out, not_299_out, not_300_out, not_301_out, not_302_out,
       not_303_out, not_304_out, not_305_out, not_306_out, not_307_out, not_308_out, not_309_out,
       not_310_out, not_311_out, not_312_out, not_313_out, not_314_out, not_315_out, not_316_out,
       not_317_out, not_318_out, not_319_out, not_320_out, not_321_out, not_322_out, not_323_out,
       not_324_out, not_325_out, not_326_out, not_327_out, not_328_out, not_329_out, not_330_out,
       not_331_out, not_332_out, not_333_out, not_334_out, not_335_out, not_336_out, not_337_out,
       not_338_out, not_339_out, not_340_out, not_341_out, not_342_out, not_343_out, or_3_out, or_4_out,
       or_5_out, or_6_out;

  not not_1 (not_1_out, in_1[3]);
  not not_2 (not_2_out, in_1[2]);
  not not_3 (not_3_out, in_1[1]);
  not not_4 (not_4_out, in_1[0]);
  not not_5 (not_5_out, in_1[3]);
  not not_6 (not_6_out, in_1[2]);
  not not_7 (not_7_out, in_1[1]);
  not not_8 (not_8_out, in_2[1]);
  not not_9 (not_9_out, in_1[3]);
  not not_10 (not_10_out, in_1[2]);
  not not_11 (not_11_out, in_1[1]);
  not not_12 (not_12_out, in_2[0]);
  not not_13 (not_13_out, in_1[3]);
  not not_14 (not_14_out, in_1[2]);
  not not_15 (not_15_out, in_1[0]);
  not not_16 (not_16_out, in_2[1]);
  not not_17 (not_17_out, in_1[3]);
  not not_18 (not_18_out, in_1[2]);
  not not_19 (not_19_out, in_2[2]);
  not not_20 (not_20_out, in_1[3]);
  not not_21 (not_21_out, in_1[2]);
  not not_22 (not_22_out, in_2[1]);
  not not_23 (not_23_out, in_2[0]);
  not not_24 (not_24_out, in_1[3]);
  not not_25 (not_25_out, in_1[1]);
  not not_26 (not_26_out, in_1[0]);
  not not_27 (not_27_out, in_2[2]);
  not not_28 (not_28_out, in_1[3]);
  not not_29 (not_29_out, in_1[1]);
  not not_30 (not_30_out, in_2[2]);
  not not_31 (not_31_out, in_2[1]);
  not not_32 (not_32_out, in_1[3]);
  not not_33 (not_33_out, in_1[1]);
  not not_34 (not_34_out, in_2[2]);
  not not_35 (not_35_out, in_2[0]);
  not not_36 (not_36_out, in_1[3]);
  not not_37 (not_37_out, in_1[0]);
  not not_38 (not_38_out, in_2[2]);
  not not_39 (not_39_out, in_2[1]);
  not not_40 (not_40_out, in_2[2]);
  not not_41 (not_41_out, in_2[1]);
  not not_42 (not_42_out, in_2[0]);
  not not_43 (not_43_out, in_1[2]);
  not not_44 (not_44_out, in_1[1]);
  not not_45 (not_45_out, in_1[0]);
  not not_46 (not_46_out, in_2[3]);
  not not_47 (not_47_out, in_1[2]);
  not not_48 (not_48_out, in_1[1]);
  not not_49 (not_49_out, in_2[3]);
  not not_50 (not_50_out, in_2[1]);
  not not_51 (not_51_out, in_1[2]);
  not not_52 (not_52_out, in_1[1]);
  not not_53 (not_53_out, in_2[3]);
  not not_54 (not_54_out, in_2[0]);
  not not_55 (not_55_out, in_1[2]);
  not not_56 (not_56_out, in_1[0]);
  not not_57 (not_57_out, in_2[3]);
  not not_58 (not_58_out, in_2[1]);
  not not_59 (not_59_out, in_1[2]);
  not not_60 (not_60_out, in_2[3]);
  not not_61 (not_61_out, in_2[2]);
  not not_62 (not_62_out, in_1[2]);
  not not_63 (not_63_out, in_2[3]);
  not not_64 (not_64_out, in_2[1]);
  not not_65 (not_65_out, in_2[0]);
  not not_66 (not_66_out, in_1[1]);
  not not_67 (not_67_out, in_1[0]);
  not not_68 (not_68_out, in_2[3]);
  not not_69 (not_69_out, in_2[2]);
  not not_70 (not_70_out, in_1[1]);
  not not_71 (not_71_out, in_2[3]);
  not not_72 (not_72_out, in_2[2]);
  not not_73 (not_73_out, in_2[1]);
  not not_74 (not_74_out, in_1[1]);
  not not_75 (not_75_out, in_2[3]);
  not not_76 (not_76_out, in_2[2]);
  not not_77 (not_77_out, in_2[0]);
  not not_78 (not_78_out, in_1[0]);
  not not_79 (not_79_out, in_2[3]);
  not not_80 (not_80_out, in_2[2]);
  not not_81 (not_81_out, in_2[1]);
  not not_82 (not_82_out, in_2[2]);
  not not_83 (not_83_out, in_2[1]);
  not not_84 (not_84_out, in_2[0]);
  not not_85 (not_85_out, in_1[3]);
  not not_86 (not_86_out, in_1[2]);
  not not_87 (not_87_out, in_1[1]);
  not not_88 (not_88_out, in_1[0]);
  not not_89 (not_89_out, in_2[2]);
  not not_90 (not_90_out, in_2[1]);
  not not_91 (not_91_out, in_1[3]);
  not not_92 (not_92_out, in_2[3]);
  not not_93 (not_93_out, in_1[3]);
  not not_94 (not_94_out, in_2[3]);
  not not_95 (not_95_out, in_1[3]);
  not not_96 (not_96_out, in_2[3]);
  not not_97 (not_97_out, in_1[3]);
  not not_98 (not_98_out, in_2[3]);
  not not_99 (not_99_out, in_1[2]);
  not not_100 (not_100_out, in_1[1]);
  not not_101 (not_101_out, in_1[0]);
  not not_102 (not_102_out, in_2[3]);
  not not_103 (not_103_out, in_2[2]);
  not not_104 (not_104_out, in_2[1]);
  not not_105 (not_105_out, in_2[0]);
  not not_106 (not_106_out, in_1[2]);
  not not_107 (not_107_out, in_1[0]);
  not not_108 (not_108_out, in_2[0]);
  not not_109 (not_109_out, in_1[1]);
  not not_110 (not_110_out, in_1[0]);
  not not_111 (not_111_out, in_2[1]);
  not not_112 (not_112_out, in_2[0]);
  not not_113 (not_113_out, in_1[0]);
  not not_114 (not_114_out, in_2[2]);
  not not_115 (not_115_out, in_2[0]);
  not not_116 (not_116_out, in_1[3]);
  not not_117 (not_117_out, in_1[2]);
  not not_118 (not_118_out, in_1[1]);
  not not_119 (not_119_out, in_1[0]);
  not not_120 (not_120_out, in_2[3]);
  not not_121 (not_121_out, in_1[3]);
  not not_122 (not_122_out, in_1[2]);
  not not_123 (not_123_out, in_1[1]);
  not not_124 (not_124_out, in_2[3]);
  not not_125 (not_125_out, in_2[1]);
  not not_126 (not_126_out, in_1[3]);
  not not_127 (not_127_out, in_1[2]);
  not not_128 (not_128_out, in_1[1]);
  not not_129 (not_129_out, in_2[3]);
  not not_130 (not_130_out, in_2[0]);
  not not_131 (not_131_out, in_1[3]);
  not not_132 (not_132_out, in_1[2]);
  not not_133 (not_133_out, in_1[0]);
  not not_134 (not_134_out, in_2[3]);
  not not_135 (not_135_out, in_2[1]);
  not not_136 (not_136_out, in_1[3]);
  not not_137 (not_137_out, in_1[2]);
  not not_138 (not_138_out, in_2[3]);
  not not_139 (not_139_out, in_2[1]);
  not not_140 (not_140_out, in_2[0]);
  not not_141 (not_141_out, in_1[2]);
  not not_142 (not_142_out, in_1[1]);
  not not_143 (not_143_out, in_1[0]);
  not not_144 (not_144_out, in_2[1]);
  not not_145 (not_145_out, in_2[0]);
  not not_146 (not_146_out, in_1[2]);
  not not_147 (not_147_out, in_2[2]);
  not not_148 (not_148_out, in_2[1]);
  not not_149 (not_149_out, in_1[2]);
  not not_150 (not_150_out, in_1[1]);
  not not_151 (not_151_out, in_2[2]);
  not not_152 (not_152_out, in_1[2]);
  not not_153 (not_153_out, in_1[1]);
  not not_154 (not_154_out, in_2[2]);
  not not_155 (not_155_out, in_1[2]);
  not not_156 (not_156_out, in_2[2]);
  not not_157 (not_157_out, in_2[1]);
  not not_158 (not_158_out, in_1[3]);
  not not_159 (not_159_out, in_1[2]);
  not not_160 (not_160_out, in_2[3]);
  not not_161 (not_161_out, in_2[2]);
  not not_162 (not_162_out, in_1[2]);
  not not_163 (not_163_out, in_1[0]);
  not not_164 (not_164_out, in_2[2]);
  not not_165 (not_165_out, in_2[0]);
  not not_166 (not_166_out, in_1[2]);
  not not_167 (not_167_out, in_2[2]);
  not not_168 (not_168_out, in_2[1]);
  not not_169 (not_169_out, in_1[3]);
  not not_170 (not_170_out, in_1[1]);
  not not_171 (not_171_out, in_1[0]);
  not not_172 (not_172_out, in_2[3]);
  not not_173 (not_173_out, in_2[2]);
  not not_174 (not_174_out, in_1[3]);
  not not_175 (not_175_out, in_1[1]);
  not not_176 (not_176_out, in_2[3]);
  not not_177 (not_177_out, in_2[2]);
  not not_178 (not_178_out, in_2[1]);
  not not_179 (not_179_out, in_1[3]);
  not not_180 (not_180_out, in_1[1]);
  not not_181 (not_181_out, in_2[3]);
  not not_182 (not_182_out, in_2[2]);
  not not_183 (not_183_out, in_2[0]);
  not not_184 (not_184_out, in_1[3]);
  not not_185 (not_185_out, in_1[0]);
  not not_186 (not_186_out, in_2[3]);
  not not_187 (not_187_out, in_2[2]);
  not not_188 (not_188_out, in_2[1]);
  not not_189 (not_189_out, in_1[3]);
  not not_190 (not_190_out, in_2[3]);
  not not_191 (not_191_out, in_2[2]);
  not not_192 (not_192_out, in_2[1]);
  not not_193 (not_193_out, in_2[0]);
  not not_194 (not_194_out, in_1[1]);
  not not_195 (not_195_out, in_1[0]);
  not not_196 (not_196_out, in_2[2]);
  not not_197 (not_197_out, in_2[1]);
  not not_198 (not_198_out, in_2[0]);
  not not_199 (not_199_out, in_1[1]);
  not not_200 (not_200_out, in_1[3]);
  not not_201 (not_201_out, in_1[0]);
  not not_202 (not_202_out, in_2[0]);
  not not_203 (not_203_out, in_2[3]);
  not not_204 (not_204_out, in_2[1]);
  not not_205 (not_205_out, in_1[2]);
  not not_206 (not_206_out, in_1[1]);
  not not_207 (not_207_out, in_2[2]);
  not not_208 (not_208_out, in_1[2]);
  not not_209 (not_209_out, in_1[1]);
  not not_210 (not_210_out, in_2[2]);
  not not_211 (not_211_out, in_1[2]);
  not not_212 (not_212_out, in_1[1]);
  not not_213 (not_213_out, in_2[2]);
  not not_214 (not_214_out, in_1[2]);
  not not_215 (not_215_out, in_1[0]);
  not not_216 (not_216_out, in_2[2]);
  not not_217 (not_217_out, in_2[0]);
  not not_218 (not_218_out, in_1[2]);
  not not_219 (not_219_out, in_2[2]);
  not not_220 (not_220_out, in_2[1]);
  not not_221 (not_221_out, in_1[2]);
  not not_222 (not_222_out, in_1[2]);
  not not_223 (not_223_out, in_1[1]);
  not not_224 (not_224_out, in_1[1]);
  not not_225 (not_225_out, in_1[1]);
  not not_226 (not_226_out, in_2[2]);
  not not_227 (not_227_out, in_2[1]);
  not not_228 (not_228_out, in_2[2]);
  not not_229 (not_229_out, in_1[3]);
  not not_230 (not_230_out, in_1[1]);
  not not_231 (not_231_out, in_1[0]);
  not not_232 (not_232_out, in_2[3]);
  not not_233 (not_233_out, in_1[1]);
  not not_234 (not_234_out, in_1[0]);
  not not_235 (not_235_out, in_2[0]);
  not not_236 (not_236_out, in_1[2]);
  not not_237 (not_237_out, in_1[1]);
  not not_238 (not_238_out, in_2[1]);
  not not_239 (not_239_out, in_1[1]);
  not not_240 (not_240_out, in_2[2]);
  not not_241 (not_241_out, in_2[1]);
  not not_242 (not_242_out, in_1[1]);
  not not_243 (not_243_out, in_1[0]);
  not not_244 (not_244_out, in_2[0]);
  not not_245 (not_245_out, in_1[1]);
  not not_246 (not_246_out, in_2[1]);
  not not_247 (not_247_out, in_1[3]);
  not not_248 (not_248_out, in_1[1]);
  not not_249 (not_249_out, in_2[3]);
  not not_250 (not_250_out, in_2[0]);
  not not_251 (not_251_out, in_1[2]);
  not not_252 (not_252_out, in_1[1]);
  not not_253 (not_253_out, in_2[1]);
  not not_254 (not_254_out, in_1[1]);
  not not_255 (not_255_out, in_2[2]);
  not not_256 (not_256_out, in_2[1]);
  not not_257 (not_257_out, in_1[3]);
  not not_258 (not_258_out, in_1[0]);
  not not_259 (not_259_out, in_2[3]);
  not not_260 (not_260_out, in_2[1]);
  not not_261 (not_261_out, in_1[3]);
  not not_262 (not_262_out, in_2[3]);
  not not_263 (not_263_out, in_2[1]);
  not not_264 (not_264_out, in_2[0]);
  not not_265 (not_265_out, in_1[0]);
  not not_266 (not_266_out, in_2[1]);
  not not_267 (not_267_out, in_2[0]);
  not not_268 (not_268_out, in_1[2]);
  not not_269 (not_269_out, in_2[2]);
  not not_270 (not_270_out, in_1[2]);
  not not_271 (not_271_out, in_2[2]);
  not not_272 (not_272_out, in_1[1]);
  not not_273 (not_273_out, in_1[0]);
  not not_274 (not_274_out, in_2[0]);
  not not_275 (not_275_out, in_1[3]);
  not not_276 (not_276_out, in_1[1]);
  not not_277 (not_277_out, in_1[0]);
  not not_278 (not_278_out, in_1[3]);
  not not_279 (not_279_out, in_1[1]);
  not not_280 (not_280_out, in_2[0]);
  not not_281 (not_281_out, in_1[1]);
  not not_282 (not_282_out, in_1[0]);
  not not_283 (not_283_out, in_2[3]);
  not not_284 (not_284_out, in_1[1]);
  not not_285 (not_285_out, in_2[3]);
  not not_286 (not_286_out, in_2[0]);
  not not_287 (not_287_out, in_1[3]);
  not not_288 (not_288_out, in_1[0]);
  not not_289 (not_289_out, in_2[1]);
  not not_290 (not_290_out, in_1[3]);
  not not_291 (not_291_out, in_2[1]);
  not not_292 (not_292_out, in_2[0]);
  not not_293 (not_293_out, in_1[0]);
  not not_294 (not_294_out, in_2[3]);
  not not_295 (not_295_out, in_2[1]);
  not not_296 (not_296_out, in_2[3]);
  not not_297 (not_297_out, in_2[1]);
  not not_298 (not_298_out, in_2[0]);
  not not_299 (not_299_out, in_1[2]);
  not not_300 (not_300_out, in_2[2]);
  not not_301 (not_301_out, in_1[2]);
  not not_302 (not_302_out, in_2[2]);
  not not_303 (not_303_out, in_1[0]);
  not not_304 (not_304_out, in_2[0]);
  and and_1 (and_1_out, not_1_out, not_2_out, not_3_out, not_4_out, in_2[3]);
  and and_2 (and_2_out, not_5_out, not_6_out, not_7_out, in_2[3], not_8_out);
  and and_3 (and_3_out, not_9_out, not_10_out, not_11_out, in_2[3], not_12_out);
  and and_4 (and_4_out, not_13_out, not_14_out, not_15_out, in_2[3], not_16_out);
  and and_5 (and_5_out, not_17_out, not_18_out, in_2[3], not_19_out);
  and and_6 (and_6_out, not_20_out, not_21_out, in_2[3], not_22_out, not_23_out);
  and and_7 (and_7_out, not_24_out, not_25_out, not_26_out, in_2[3], not_27_out);
  and and_8 (and_8_out, not_28_out, not_29_out, in_2[3], not_30_out, not_31_out);
  and and_9 (and_9_out, not_32_out, not_33_out, in_2[3], not_34_out, not_35_out);
  and and_10 (and_10_out, not_36_out, not_37_out, in_2[3], not_38_out, not_39_out);
  and and_11 (and_11_out, in_2[3], not_40_out, not_41_out, not_42_out);
  and and_12 (and_12_out, in_1[3], not_43_out, not_44_out, not_45_out, not_46_out);
  and and_13 (and_13_out, in_1[3], not_47_out, not_48_out, not_49_out, not_50_out);
  and and_14 (and_14_out, in_1[3], not_51_out, not_52_out, not_53_out, not_54_out);
  and and_15 (and_15_out, in_1[3], not_55_out, not_56_out, not_57_out, not_58_out);
  and and_16 (and_16_out, in_1[3], not_59_out, not_60_out, not_61_out);
  and and_17 (and_17_out, in_1[3], not_62_out, not_63_out, not_64_out, not_65_out);
  and and_18 (and_18_out, in_1[3], not_66_out, not_67_out, not_68_out, not_69_out);
  and and_19 (and_19_out, in_1[3], not_70_out, not_71_out, not_72_out, not_73_out);
  and and_20 (and_20_out, in_1[3], not_74_out, not_75_out, not_76_out, not_77_out);
  and and_21 (and_21_out, in_1[3], not_78_out, not_79_out, not_80_out, not_81_out);
  and and_22 (and_22_out, in_1[3], not_82_out, not_83_out, not_84_out);
  and and_23 (and_23_out, in_1[3], in_1[0], in_2[3]);
  and and_24 (and_24_out, in_1[3], in_1[1], in_2[3]);
  and and_25 (and_25_out, in_1[3], in_1[2], in_2[3]);
  not not_305 (not_305_out, in_1[3]);
  not not_306 (not_306_out, in_2[3]);
  not not_307 (not_307_out, in_1[3]);
  not not_308 (not_308_out, in_2[3]);
  not not_309 (not_309_out, in_1[3]);
  not not_310 (not_310_out, in_2[3]);
  not not_311 (not_311_out, in_1[1]);
  not not_312 (not_312_out, in_2[2]);
  not not_313 (not_313_out, in_1[2]);
  not not_314 (not_314_out, in_2[2]);
  not not_315 (not_315_out, in_1[2]);
  not not_316 (not_316_out, in_1[1]);
  not not_317 (not_317_out, in_1[2]);
  not not_318 (not_318_out, in_2[1]);
  not not_319 (not_319_out, in_1[2]);
  not not_320 (not_320_out, in_1[1]);
  not not_321 (not_321_out, in_2[2]);
  not not_322 (not_322_out, in_2[1]);
  not not_323 (not_323_out, in_1[1]);
  not not_324 (not_324_out, in_2[2]);
  and and_26 (and_26_out, not_116_out, not_117_out, not_118_out, not_119_out, not_120_out, in_2[2]);
  and and_27 (and_27_out, not_121_out, not_122_out, not_123_out, not_124_out, in_2[2], not_125_out);
  and and_28 (and_28_out, not_126_out, not_127_out, not_128_out, not_129_out, in_2[2], not_130_out);
  and and_29 (and_29_out, not_131_out, not_132_out, not_133_out, not_134_out, in_2[2], not_135_out);
  and and_30 (and_30_out, not_136_out, not_137_out, not_138_out, in_2[2], not_139_out, not_140_out);
  and and_31 (and_31_out, not_141_out, not_142_out, not_143_out, in_2[2], not_144_out, not_145_out);
  and and_32 (and_32_out, not_146_out, in_2[3], not_147_out, not_148_out, in_2[0]);
  and and_33 (and_33_out, not_149_out, not_150_out, in_2[3], not_151_out, in_2[1]);
  and and_34 (and_34_out, not_152_out, not_153_out, in_1[0], not_154_out, in_2[1], in_2[0]);
  and and_35 (and_35_out, not_155_out, in_1[0], in_2[3], not_156_out, not_157_out);
  and and_36 (and_36_out, not_158_out, not_159_out, in_1[1], not_160_out, not_161_out, in_2[1]);
  and and_37 (and_37_out, not_162_out, in_1[1], not_163_out, in_2[3], not_164_out, not_165_out);
  and and_38 (and_38_out, not_166_out, in_1[1], in_1[0], not_167_out, not_168_out, in_2[0]);
  and and_39 (and_39_out, not_169_out, in_1[2], not_170_out, not_171_out, not_172_out, not_173_out);
  and and_40 (and_40_out, not_174_out, in_1[2], not_175_out, not_176_out, not_177_out, not_178_out);
  and and_41 (and_41_out, not_179_out, in_1[2], not_180_out, not_181_out, not_182_out, not_183_out);
  and and_42 (and_42_out, not_184_out, in_1[2], not_185_out, not_186_out, not_187_out, not_188_out);
  and and_43 (and_43_out, not_189_out, in_1[2], not_190_out, not_191_out, not_192_out, not_193_out);
  and and_44 (and_44_out, in_1[2], not_194_out, not_195_out, not_196_out, not_197_out, not_198_out);
  and and_45 (and_45_out, in_1[2], not_199_out, in_1[0], in_2[2], in_2[1], in_2[0]);
  and and_46 (and_46_out, not_200_out, in_1[2], in_1[1], in_2[2], in_2[1]);
  and and_47 (and_47_out, in_1[2], in_1[1], not_201_out, in_2[2], in_2[1], not_202_out);
  and and_48 (and_48_out, in_1[2], in_1[1], not_203_out, in_2[2], in_2[1]);
  and and_49 (and_49_out, in_1[2], in_1[1], in_1[0], in_2[2], not_204_out, in_2[0]);
  and and_50 (and_50_out, in_1[3], not_205_out, not_206_out, not_207_out, in_2[0]);
  and and_51 (and_51_out, in_1[3], not_208_out, not_209_out, not_210_out, in_2[1]);
  and and_52 (and_52_out, in_1[3], not_211_out, not_212_out, in_1[0], not_213_out);
  and and_53 (and_53_out, in_1[3], not_214_out, in_1[1], not_215_out, not_216_out, not_217_out);
  and and_54 (and_54_out, in_1[3], not_218_out, in_1[1], not_219_out, not_220_out);
  and and_55 (and_55_out, in_1[3], not_221_out, in_1[1], in_2[3], in_2[2], in_2[1], in_2[0]);
  and and_56 (and_56_out, in_1[3], not_222_out, in_1[1], in_1[0], in_2[3], in_2[2], in_2[1]);
  and and_57 (and_57_out, in_1[3], in_1[2], not_223_out, in_2[3], in_2[2], in_2[0]);
  and and_58 (and_58_out, in_1[3], in_1[2], not_224_out, in_2[3], in_2[2], in_2[1]);
  and and_59 (and_59_out, in_1[3], in_1[2], not_225_out, in_1[0], in_2[3], in_2[2]);
  and and_60 (and_60_out, in_1[3], in_1[2], in_1[1], in_2[3], not_226_out, in_2[1], in_2[0]);
  and and_61 (and_61_out, in_1[3], in_1[2], in_1[1], in_2[3], in_2[2], not_227_out);
  and and_62 (and_62_out, in_1[3], in_1[2], in_1[1], in_1[0], in_2[3], not_228_out, in_2[1]);
  and and_63 (and_63_out, not_229_out, not_230_out, not_231_out, not_232_out, in_2[1], in_2[0]);
  and and_64 (and_64_out, not_233_out, not_234_out, in_2[2], in_2[1], not_235_out);
  and and_65 (and_65_out, not_236_out, not_237_out, in_2[3], not_238_out, in_2[0]);
  and and_66 (and_66_out, not_239_out, in_2[3], not_240_out, not_241_out, in_2[0]);
  and and_67 (and_67_out, not_242_out, not_243_out, in_2[3], in_2[1], not_244_out);
  and and_68 (and_68_out, not_245_out, in_1[0], not_246_out, in_2[0]);
  and and_69 (and_69_out, not_247_out, not_248_out, in_1[0], not_249_out, in_2[1], not_250_out);
  and and_70 (and_70_out, not_251_out, not_252_out, in_1[0], in_2[3], not_253_out);
  and and_71 (and_71_out, not_254_out, in_1[0], in_2[3], not_255_out, not_256_out);
  and and_72 (and_72_out, not_257_out, in_1[1], not_258_out, not_259_out, not_260_out);
  and and_73 (and_73_out, not_261_out, in_1[1], not_262_out, not_263_out, not_264_out);
  and and_74 (and_74_out, in_1[1], not_265_out, not_266_out, not_267_out);
  and and_75 (and_75_out, not_268_out, in_1[1], in_2[3], not_269_out, in_2[1], in_2[0]);
  and and_76 (and_76_out, in_1[1], in_1[0], in_2[1], in_2[0]);
  and and_77 (and_77_out, not_270_out, in_1[1], in_1[0], in_2[3], not_271_out, in_2[1]);
  and and_78 (and_78_out, in_1[2], not_272_out, not_273_out, in_2[1], not_274_out);
  and and_79 (and_79_out, not_275_out, in_1[2], not_276_out, not_277_out, in_2[2], in_2[1]);
  and and_80 (and_80_out, not_278_out, in_1[2], not_279_out, in_2[2], in_2[1], not_280_out);
  not not_325 (not_325_out, in_1[2]);
  not not_326 (not_326_out, in_1[1]);
  not not_327 (not_327_out, in_2[1]);
  not not_328 (not_328_out, in_1[1]);
  not not_329 (not_329_out, in_2[2]);
  not not_330 (not_330_out, in_2[1]);
  not not_331 (not_331_out, in_1[1]);
  not not_332 (not_332_out, in_1[0]);
  not not_333 (not_333_out, in_2[0]);
  not not_334 (not_334_out, in_1[1]);
  not not_335 (not_335_out, in_2[1]);
  not not_336 (not_336_out, in_1[2]);
  not not_337 (not_337_out, in_1[1]);
  not not_338 (not_338_out, in_2[1]);
  not not_339 (not_339_out, in_1[1]);
  not not_340 (not_340_out, in_2[2]);
  not not_341 (not_341_out, in_2[1]);
  not not_342 (not_342_out, in_1[1]);
  not not_343 (not_343_out, in_2[1]);
  and and_81 (and_81_out, not_303_out, in_2[0]);
  and and_82 (and_82_out, in_1[0], not_304_out);
  and and_83 (and_83_out, not_85_out, not_86_out, not_87_out, not_88_out, in_2[3], not_89_out, not_90_out);
  and and_84 (and_84_out, not_91_out, in_1[0], not_92_out, in_2[2], in_2[1], in_2[0]);
  and and_85 (and_85_out, not_305_out, in_1[1], not_306_out, in_2[2], in_2[1]);
  and and_86 (and_86_out, not_93_out, in_1[1], in_1[0], not_94_out, in_2[2], in_2[0]);
  and and_87 (and_87_out, not_307_out, in_1[2], not_308_out, in_2[2]);
  and and_88 (and_88_out, not_95_out, in_1[2], in_1[0], not_96_out, in_2[1], in_2[0]);
  and and_89 (and_89_out, not_309_out, in_1[2], in_1[1], not_310_out, in_2[1]);
  and and_90 (and_90_out, not_97_out, in_1[2], in_1[1], in_1[0], not_98_out, in_2[0]);
  and and_91 (and_91_out, in_1[3], not_99_out, not_100_out, not_101_out, not_102_out, not_103_out, not_104_out, not_105_out);
  and and_92 (and_92_out, in_1[3], not_311_out, in_2[3], not_312_out, in_2[0]);
  and and_93 (and_93_out, in_1[3], not_313_out, in_2[3], not_314_out, in_2[1]);
  and and_94 (and_94_out, in_1[3], not_315_out, not_316_out, in_2[3], in_2[2]);
  and and_95 (and_95_out, in_1[3], not_317_out, in_2[3], in_2[2], not_318_out);
  and and_96 (and_96_out, in_1[3], not_319_out, not_320_out, in_1[0], in_2[3]);
  and and_97 (and_97_out, in_1[3], not_106_out, in_1[1], not_107_out, in_2[3], not_108_out);
  and and_98 (and_98_out, in_1[3], in_1[1], in_2[3], not_321_out, not_322_out);
  and and_99 (and_99_out, in_1[3], in_1[2], not_109_out, not_110_out, in_2[3], not_111_out, not_112_out);
  and and_100 (and_100_out, in_1[3], in_1[2], not_323_out, in_2[3], not_324_out);
  and and_101 (and_101_out, in_1[3], in_1[2], not_113_out, in_2[3], not_114_out, not_115_out);
  and and_102 (and_102_out, in_1[2], not_281_out, not_282_out, not_283_out, in_2[2], in_2[1]);
  and and_103 (and_103_out, in_1[2], not_284_out, not_285_out, in_2[2], in_2[1], not_286_out);
  and and_104 (and_104_out, not_287_out, in_1[2], in_1[1], not_288_out, in_2[2], not_289_out);
  and and_105 (and_105_out, not_290_out, in_1[2], in_1[1], in_2[2], not_291_out, not_292_out);
  and and_106 (and_106_out, in_1[2], in_1[1], not_293_out, not_294_out, in_2[2], not_295_out);
  and and_107 (and_107_out, in_1[2], in_1[1], not_296_out, in_2[2], not_297_out, not_298_out);
  and and_108 (and_108_out, in_1[3], not_325_out, not_326_out, not_327_out, in_2[0]);
  and and_109 (and_109_out, in_1[3], not_328_out, not_329_out, not_330_out, in_2[0]);
  and and_110 (and_110_out, in_1[3], not_331_out, not_332_out, in_2[1], not_333_out);
  and and_111 (and_111_out, in_1[3], not_334_out, in_2[3], not_335_out, in_2[0]);
  and and_112 (and_112_out, in_1[3], not_336_out, not_337_out, in_1[0], not_338_out);
  and and_113 (and_113_out, in_1[3], not_339_out, in_1[0], not_340_out, not_341_out);
  and and_114 (and_114_out, in_1[3], not_342_out, in_1[0], in_2[3], not_343_out);
  and and_115 (and_115_out, in_1[3], not_299_out, in_1[1], not_300_out, in_2[1], in_2[0]);
  and and_116 (and_116_out, in_1[3], in_1[1], in_2[3], in_2[1], in_2[0]);
  and and_117 (and_117_out, in_1[3], not_301_out, in_1[1], in_1[0], not_302_out, in_2[1]);
  and and_118 (and_118_out, in_1[3], in_1[1], in_1[0], in_2[3], in_2[1]);
  or or_1 (out_4[0], and_81_out, and_82_out);
  or or_2 (out_4[3], and_83_out, and_84_out, and_85_out, and_86_out, and_87_out, and_88_out, and_89_out, and_90_out, and_91_out, and_92_out, and_93_out, and_94_out, and_95_out, and_96_out, and_97_out, and_98_out, and_99_out, and_100_out, and_101_out);
  or or_3 (or_3_out, and_26_out, and_27_out, and_28_out, and_29_out, and_30_out, and_31_out, and_32_out, and_33_out, and_34_out, and_35_out, and_36_out, and_37_out, and_38_out, and_39_out, and_40_out, and_41_out, and_42_out, and_43_out, and_44_out);
  or or_4 (or_4_out, and_45_out, and_46_out, and_47_out, and_48_out, and_49_out, and_50_out, and_51_out, and_52_out, and_53_out, and_54_out, and_55_out, and_56_out, and_57_out, and_58_out, and_59_out, and_60_out, and_61_out, and_62_out);
  or or_5 (or_5_out, and_63_out, and_64_out, and_65_out, and_66_out, and_67_out, and_68_out, and_69_out, and_70_out, and_71_out, and_72_out, and_73_out, and_74_out, and_75_out, and_76_out, and_77_out, and_78_out, and_79_out, and_80_out);
  or or_6 (or_6_out, and_102_out, and_103_out, and_104_out, and_105_out, and_106_out, and_107_out, and_108_out, and_109_out, and_110_out, and_111_out, and_112_out, and_113_out, and_114_out, and_115_out, and_116_out, and_117_out, and_118_out);
  or or_7 (sinal, and_1_out, and_2_out, and_3_out, and_4_out, and_5_out, and_6_out, and_7_out, and_8_out, and_9_out, and_10_out, and_11_out, and_12_out, and_13_out, and_14_out, and_15_out, and_16_out, and_17_out, and_18_out, and_19_out, and_20_out, and_21_out, and_22_out, and_23_out, and_24_out, and_25_out);
  or or_8 (out_4[2], or_3_out, or_4_out);
  or or_9 (out_4[1], or_5_out, or_6_out);
  Hex_Digit_Display hex_digit_display_1 (.value(out_4));  // open: dp
endmodule

module \Seleção  (
  input  [3:0] In1,
  input  [3:0] In2,
  input  \Próximo ,
  input  ATZ,
  input  BTZ,
  input  Chutar,
  input  Iniciar,
  input  Reset,
  output [3:0] Out1,
  output A_Jogando,
  output B_Jogando,
  output X,
  output Y,
  output Negativo___A,
  output [3:0] Out2,
  output Negativo___B,
  output [3:0] X_final,
  output X_final_negativo,
  output [3:0] Y_final,
  output Y_final_negativo,
  output Igual,
  output Maior,
  output Menor,
  output Acertou,
  output [3:0] Placar_A,
  output _15pontos,
  output [3:0] Placar_B
);

  wire and_1_out, and_2_out, and_3_out, and_4_out, and_5_out, and_6_out, comparador_1_i0___i1,
       comparador_2_i0___i1, demultiplexer_1_out1, demultiplexer_1_out2, demultiplexer_1_out4,
       demultiplexer_1_out5, fazacertar_1_s1, not_1_out, not_2_out, not_3_out, not_4_out, or_1_out, or_2_out,
       somador_7_8_1_sinal, somador_7_8_2_sinal;
  wire [2:0] cont_estados_1_out_4;
  wire [3:0] demultiplexer_2_out1, demultiplexer_2_out2, demultiplexer_2_out4, demultiplexer_2_out5,
       \gerador_aleatório_1_x_secret_number , \gerador_aleatório_1_y_secret_number , multiplexer_1_out,
       multiplexer_2_out, multiplexer_3_out, registrador_ffp_1_out_9, registrador_ffp_2_out_9,
       registrador_ffp_3_out_9, registrador_ffp_4_out_9, somador_7_8_1_out_4, somador_7_8_2_out_4;

  Button \u_Próximo  ();  // open: out
  Cont_estados cont_estados_1 (
    .\Próx (\Próximo ), .ATZ(ATZ), .BTZ(BTZ), .out_4(cont_estados_1_out_4[0]),
    .out_5(cont_estados_1_out_4[1]), .out_6(cont_estados_1_out_4[2]));
  or or_1 (or_1_out, Iniciar, Acertou);
  FazAcertar fazacertar_1 (
    .A1(cont_estados_1_out_4[0]), .A2(cont_estados_1_out_4[1]), .A3(cont_estados_1_out_4[2]),
    .S1(fazacertar_1_s1));
  not not_1 (not_1_out, cont_estados_1_out_4[0]);
  not not_2 (not_2_out, cont_estados_1_out_4[0]);
  not not_3 (not_3_out, cont_estados_1_out_4[1]);
  not not_4 (not_4_out, cont_estados_1_out_4[2]);
  Somador__7_8 somador_7_8_1 (
    .in_1(\gerador_aleatório_1_x_secret_number ), .in_2(\gerador_aleatório_1_y_secret_number ),
    .sinal(somador_7_8_1_sinal), .out_4(somador_7_8_1_out_4));
  \Gerador_aleatório  \gerador_aleatório_1  (
    .Puso_gerador(or_1_out), .X_Secret_Number(\gerador_aleatório_1_x_secret_number ),
    .Y_Secret_Number(\gerador_aleatório_1_y_secret_number ));
  Hex_Digit_Display hex_digit_display_1 (.value(\gerador_aleatório_1_y_secret_number ));  // open: dp
  Hex_Digit_Display hex_digit_display_2 (.value(\gerador_aleatório_1_x_secret_number ));  // open: dp
  and and_1 (and_1_out, not_1_out, cont_estados_1_out_4[1], cont_estados_1_out_4[2]);
  or or_2 (or_2_out, and_1_out, and_2_out);
  and and_2 (and_2_out, not_2_out, not_3_out, not_4_out);
  Hex_Digit_Display hex_digit_display_3 (.value(somador_7_8_1_out_4));  // open: dp
  and and_3 (and_3_out, Acertou, and_1_out);
  and and_4 (and_4_out, Acertou, and_2_out);
  XouY_AouB xouy_aoub_1 (.in_1(cont_estados_1_out_4), .X(X), .Y(Y), .A(A_Jogando), .B(B_Jogando));
  Registrador_FFP registrador_ffp_1 (
    .D3(demultiplexer_2_out4[3]), .D2(demultiplexer_2_out4[2]), .D1(demultiplexer_2_out4[1]),
    .D0(demultiplexer_2_out4[0]), .Clock(demultiplexer_1_out4), .out_9(registrador_ffp_1_out_9));  // open: Clear, Enable, Preset
  Placar placar_1 (.Clock(and_3_out), .Reset(Reset), .Enable(Iniciar), .out_4(Placar_A));
  Placar placar_2 (.Clock(and_4_out), .Reset(Reset), .Enable(Iniciar), .out_4(Placar_B));
  Hex_Digit_Display hex_digit_display_4 (.value(registrador_ffp_1_out_9));  // open: dp
  Registrador_FFP registrador_ffp_2 (
    .D3(demultiplexer_2_out2[3]), .D2(demultiplexer_2_out2[2]), .D1(demultiplexer_2_out2[1]),
    .D0(demultiplexer_2_out2[0]), .Clock(demultiplexer_1_out2), .out_9(registrador_ffp_2_out_9));  // open: Clear, Enable, Preset
  Multiplexer #(.width(4)) multiplexer_1 (
    .in0(registrador_ffp_1_out_9), .in1(registrador_ffp_3_out_9), .out(multiplexer_1_out),
    .sel(fazacertar_1_s1));  // open: en
  Button u_Chutar ();  // open: out
  Multiplexer #(.width(4)) multiplexer_2 (
    .in0(In1), .in1(In2), .out(multiplexer_2_out), .sel(cont_estados_1_out_4[0]));  // open: en
  Hex_Digit_Display hex_digit_display_5 (.value(registrador_ffp_2_out_9));  // open: dp
  Demultiplexer #(.select(3)) demultiplexer_1 (
    .out1(demultiplexer_1_out1), .out2(demultiplexer_1_out2), .out4(demultiplexer_1_out4),
    .out5(demultiplexer_1_out5), .in(Chutar), .sel(cont_estados_1_out_4), .en(1'b1));  // open: out0, out3, out6, out7
  Multiplexer #(.width(4)) multiplexer_3 (
    .in0(registrador_ffp_2_out_9), .in1(registrador_ffp_4_out_9), .out(multiplexer_3_out),
    .sel(fazacertar_1_s1));  // open: en
  Somador__7_8 somador_7_8_2 (
    .in_1(multiplexer_3_out), .in_2(multiplexer_1_out), .sinal(somador_7_8_2_sinal),
    .out_4(somador_7_8_2_out_4));
  Hex_Digit_Display hex_digit_display_6 (.value(somador_7_8_2_out_4));  // open: dp
  Demultiplexer #(.select(3), .width(4)) demultiplexer_2 (
    .out1(demultiplexer_2_out1), .out2(demultiplexer_2_out2), .out4(demultiplexer_2_out4),
    .out5(demultiplexer_2_out5), .in(multiplexer_2_out), .sel(cont_estados_1_out_4), .en(1'b1));  // open: out0, out3, out6, out7
  LED Negativo (.in(somador_7_8_2_sinal));
  and and_5 (and_5_out, Placar_A[3], Placar_A[2], Placar_A[1], Placar_A[0]);
  and and_6 (and_6_out, Placar_B[3], Placar_B[2], Placar_B[1], Placar_B[0]);
  Converte converte_1 (.A3(In1[3]), .A2(In1[2]), .A1(In1[1]), .A0(In1[0]), .\Saída (Out1), .Negativo(Negativo___A));
  Converte converte_2 (.A3(In2[3]), .A2(In2[2]), .A1(In2[1]), .A0(In2[0]), .\Saída (Out2), .Negativo(Negativo___B));
  Registrador_FFP registrador_ffp_3 (
    .D3(demultiplexer_2_out1[3]), .D2(demultiplexer_2_out1[2]), .D1(demultiplexer_2_out1[1]),
    .D0(demultiplexer_2_out1[0]), .Clock(demultiplexer_1_out1), .out_9(registrador_ffp_3_out_9));  // open: Clear, Enable, Preset
  Hex_Digit_Display hex_digit_display_7 (.value(registrador_ffp_3_out_9));  // open: dp
  Comparador comparador_1 (
    .\N_mág (\gerador_aleatório_1_x_secret_number ), .Chute(multiplexer_1_out), .Ctrl(or_2_out),
    .I0___I1(comparador_1_i0___i1));  // open: Maior, Menor
  Comparador comparador_2 (
    .\N_mág (\gerador_aleatório_1_y_secret_number ), .Chute(multiplexer_3_out), .Ctrl(or_2_out),
    .I0___I1(comparador_2_i0___i1));  // open: Maior, Menor
  or or_3 (_15pontos, and_5_out, and_6_out);
  Registrador_FFP registrador_ffp_4 (
    .D3(demultiplexer_2_out5[3]), .D2(demultiplexer_2_out5[2]), .D1(demultiplexer_2_out5[1]),
    .D0(demultiplexer_2_out5[0]), .Clock(demultiplexer_1_out5), .out_9(registrador_ffp_4_out_9));  // open: Clear, Enable, Preset
  Converte converte_3 (
    .A3(multiplexer_1_out[3]), .A2(multiplexer_1_out[2]), .A1(multiplexer_1_out[1]),
    .A0(multiplexer_1_out[0]), .\Saída (X_final), .Negativo(X_final_negativo));
  Converte converte_4 (
    .A3(multiplexer_3_out[3]), .A2(multiplexer_3_out[2]), .A1(multiplexer_3_out[1]),
    .A0(multiplexer_3_out[0]), .\Saída (Y_final), .Negativo(Y_final_negativo));
  Compara2 compara2_1 (
    .Igual(Igual), .\N_Mág (somador_7_8_2_out_4), .Chute(somador_7_8_1_out_4), .Maior(Maior),
    .\Neg_Mág (somador_7_8_1_sinal), .Neg_Chute(somador_7_8_2_sinal), .Menor(Menor), .Ctrl(or_2_out));
  and and_7 (Acertou, comparador_1_i0___i1, comparador_2_i0___i1);
  Hex_Digit_Display hex_digit_display_8 (.value(registrador_ffp_4_out_9));  // open: dp
endmodule

module Cont_estados (
  input  \Próx ,
  input  ATZ,
  input  BTZ,
  output out_4,
  output out_5,
  output out_6
);

  wire d_ff_1_q, d_ff_2_q, d_ff_3_q;

  D_Flip_Flop d_ff_1 (.clk(\Próx ), .D(out_4), .Q(d_ff_1_q));  // open: Qn, preset, en, reset
  D_Flip_Flop d_ff_2 (.clk(\Próx ), .D(out_5), .Q(d_ff_2_q));  // open: Qn, preset, en, reset
  D_Flip_Flop d_ff_3 (.clk(\Próx ), .D(out_6), .Q(d_ff_3_q));  // open: Qn, preset, en, reset
  MaisEstados maisestados_1 (
    .S1(d_ff_1_q), .S2(d_ff_2_q), .S3(d_ff_3_q), .ATZ(ATZ), .BTZ(BTZ), .out_6(out_4), .out_7(out_5),
    .out_8(out_6));
endmodule

module \Gerador_aleatório  (
  input  Puso_gerador,
  output [3:0] X_Secret_Number,
  output [3:0] Y_Secret_Number
);

  Random #(.width(1), .trigger("falling")) random_1 (.clk(Puso_gerador), .out(X_Secret_Number[0]));  // open: next, clr
  Random #(.width(1), .trigger("falling")) random_2 (.clk(Puso_gerador), .out(X_Secret_Number[1]));  // open: next, clr
  Random #(.width(1), .trigger("falling")) random_3 (.clk(Puso_gerador), .out(X_Secret_Number[2]));  // open: next, clr
  Random #(.width(1), .trigger("falling")) random_4 (.clk(Puso_gerador), .out(X_Secret_Number[3]));  // open: next, clr
  Random #(.width(1), .trigger("falling")) random_5 (.clk(Puso_gerador), .out(Y_Secret_Number[0]));  // open: next, clr
  Random #(.width(1), .trigger("falling")) random_6 (.clk(Puso_gerador), .out(Y_Secret_Number[1]));  // open: next, clr
  Random #(.width(1), .trigger("falling")) random_7 (.clk(Puso_gerador), .out(Y_Secret_Number[2]));  // open: next, clr
  Random #(.width(1), .trigger("falling")) random_8 (.clk(Puso_gerador), .out(Y_Secret_Number[3]));  // open: next, clr
  Hex_Digit_Display hex_digit_display_1 (.value(X_Secret_Number));  // open: dp
  Hex_Digit_Display hex_digit_display_2 (.value(Y_Secret_Number));  // open: dp
endmodule

module Compara2 (
  input  [3:0] \N_Mág ,
  input  [3:0] Chute,
  input  \Neg_Mág ,
  input  Neg_Chute,
  input  Ctrl,
  output Igual,
  output Maior,
  output Menor
);

  wire and_1_out, and_2_out, comparador_1_i0___i1, comparador_1_maior, comparador_1_menor, or_1_out,
       or_2_out, xnor_1_out;

  xnor xnor_1 (xnor_1_out, \Neg_Mág , Neg_Chute);
  and and_1 (and_1_out, ~\Neg_Mág , Neg_Chute);  // AND_Gate
  and and_2 (and_2_out, \Neg_Mág , ~Neg_Chute);  // AND_Gate
  Comparador comparador_1 (
    .\N_mág (\N_Mág ), .Chute(Chute), .Ctrl(xnor_1_out), .I0___I1(comparador_1_i0___i1),
    .Maior(comparador_1_maior), .Menor(comparador_1_menor));
  and and_3 (Igual, Ctrl, comparador_1_i0___i1);
  or or_1 (or_1_out, comparador_1_menor, and_1_out);
  and and_4 (Menor, or_1_out, Ctrl);
  or or_2 (or_2_out, comparador_1_maior, and_2_out);
  and and_5 (Maior, or_2_out, Ctrl);
endmodule

module Jogo (
  input  Enable,
  input  Preset,
  input  Clear,
  input  A3,
  input  A3_2,
  input  A2,
  input  A2_2,
  input  A1,
  input  A1_2,
  input  A0,
  input  A0_2
);

  wire and_1_out, and_2_out, and_3_out, Chutar_out, clock_1_out, Configurar_2_out, Configurar_out, DM_2_out,
       DM_out, DS_2_out, DS_out, mostrador2_1_lamp_config, mostrador2_2_lamp_config, or_1_out, or_2_out,
       or_3_out, or_4_out, or_5_out, or_6_out, \Próximo_out , \seleção_1__15pontos , \seleção_1_a_jogando ,
       \seleção_1_acertou , \seleção_1_b_jogando , \seleção_1_igual , \seleção_1_maior , \seleção_1_menor ,
       \seleção_1_negativo___a , \seleção_1_negativo___b , \seleção_1_x , \seleção_1_x_final_negativo ,
       \seleção_1_y , \seleção_1_y_final_negativo , UM_2_out, UM_out, undriven, US_2_out, US_out;
  wire [3:0] mostrador2_1_dmm, mostrador2_1_dss, mostrador2_1_mum, mostrador2_1_uss, mostrador2_2_dmm,
       mostrador2_2_dss, mostrador2_2_mum, mostrador2_2_uss, \seleção_1_out1 , \seleção_1_out2 ,
       \seleção_1_placar_a , \seleção_1_placar_b , \seleção_1_x_final , \seleção_1_y_final ;

  or or_1 (or_1_out, Enable, Clear, \seleção_1__15pontos );
  Hex_Digit_Display hex_digit_display_1 (.value(mostrador2_1_dmm));  // open: dp
  Hex_Digit_Display hex_digit_display_2 (.value(mostrador2_1_mum));  // open: dp
  Mostrador2 mostrador2_1 (
    .Clear(Clear), .Enable(or_1_out), .Preset(Clear), .Configurar(or_6_out), .Clock(and_2_out),
    .DM(or_2_out), .UM(or_3_out), .DS(or_4_out), .US(or_5_out), .Lamp_Config(mostrador2_1_lamp_config),
    .MUM(mostrador2_1_mum), .DMM(mostrador2_1_dmm), .DSS(mostrador2_1_dss), .USS(mostrador2_1_uss),
    .Zerou(Clear));
  and and_1 (and_1_out, ~\seleção_1_igual , ~\seleção_1_maior , ~\seleção_1_menor );  // AND_Gate
  Hex_Digit_Display hex_digit_display_3 (.value(mostrador2_1_dss));  // open: dp
  Hex_Digit_Display hex_digit_display_4 (.value(\seleção_1_out1 ));  // open: dp
  Button UM (.out(UM_out));
  Hex_Digit_Display hex_digit_display_5 (.value(mostrador2_1_uss));  // open: dp
  LED SA (.in(\seleção_1_negativo___a ));
  LED Igual (.in(\seleção_1_igual ));
  LED Maior (.in(\seleção_1_maior ));
  Button DM (.out(DM_out));
  Button UM_2 (.out(UM_2_out));
  Button DM_2 (.out(DM_2_out));
  Button DS (.out(DS_out));
  or or_2 (or_2_out, UM_out, UM_2_out);
  or or_3 (or_3_out, DM_2_out, DM_out);
  Button Chutar (.out(Chutar_out));
  LED A_Jogando (.in(\seleção_1_a_jogando ));
  LED Menor (.in(\seleção_1_menor ));
  LED Negativo (.in(\seleção_1_x_final_negativo ));
  Hex_Digit_Display hex_digit_display_6 (.value(\seleção_1_x_final ));  // open: dp
  Button US (.out(US_out));
  Button US_2 (.out(US_2_out));
  Button DS_2 (.out(DS_2_out));
  or or_4 (or_4_out, DS_out, DS_2_out);
  or or_5 (or_5_out, US_out, US_2_out);
  LED Configurando (.in(mostrador2_1_lamp_config));
  and and_2 (and_2_out, clock_1_out, ~\seleção_1_b_jogando , and_1_out);  // AND_Gate
  Button \Próximo  (.out(\Próximo_out ));
  \Seleção  \seleção_1  (
    .Out1(\seleção_1_out1 ), .In1({A3_2, A2_2, A1_2, A0_2}), .In2({A3, A2, A1, A0}), .Out2(\seleção_1_out2 ),
    .\Próximo (\Próximo_out ), .Iniciar(or_1_out), .Igual(\seleção_1_igual ), .Maior(\seleção_1_maior ),
    .Menor(\seleção_1_menor ), .Acertou(\seleção_1_acertou ), .Chutar(Chutar_out),
    .Negativo___A(\seleção_1_negativo___a ), .Negativo___B(\seleção_1_negativo___b ),
    .A_Jogando(\seleção_1_a_jogando ), .B_Jogando(\seleção_1_b_jogando ), .X_final(\seleção_1_x_final ),
    .Y_final(\seleção_1_y_final ), .X_final_negativo(\seleção_1_x_final_negativo ),
    .Y_final_negativo(\seleção_1_y_final_negativo ), .X(\seleção_1_x ), .Y(\seleção_1_y ),
    .Placar_A(\seleção_1_placar_a ), .Placar_B(\seleção_1_placar_b ), .ATZ(undriven), .BTZ(Clear),
    ._15pontos(\seleção_1__15pontos ), .Reset(Clear));
  LED X (.in(\seleção_1_x ));
  LED Y (.in(\seleção_1_y ));
  Hex_Digit_Display hex_digit_display_7 (.value(\seleção_1_y_final ));  // open: dp
  Clock clock_1 (.out(clock_1_out));
  LED B_Jogando (.in(\seleção_1_b_jogando ));
  LED Negativo_2 (.in(\seleção_1_y_final_negativo ));
  Button Configurar (.out(Configurar_out));
  or or_6 (or_6_out, Configurar_out, Configurar_2_out);
  Hex_Digit_Display hex_digit_display_8 (.value(mostrador2_2_dmm));  // open: dp
  Mostrador2 mostrador2_2 (
    .Clear(Clear), .Enable(or_1_out), .Preset(Clear), .Configurar(or_6_out), .Clock(and_3_out),
    .DM(or_2_out), .UM(or_3_out), .DS(or_4_out), .US(or_5_out), .Lamp_Config(mostrador2_2_lamp_config),
    .MUM(mostrador2_2_mum), .DMM(mostrador2_2_dmm), .DSS(mostrador2_2_dss), .USS(mostrador2_2_uss),
    .Zerou(Clear));
  LED SB (.in(\seleção_1_negativo___b ));
  Hex_Digit_Display hex_digit_display_9 (.value(\seleção_1_out2 ));  // open: dp
  LED Acertou (.in(\seleção_1_acertou ));
  Button Configurar_2 (.out(Configurar_2_out));
  Hex_Digit_Display hex_digit_display_10 (.value(mostrador2_2_mum));  // open: dp
  Hex_Digit_Display hex_digit_display_11 (.value(mostrador2_2_dss));  // open: dp
  Hex_Digit_Display hex_digit_display_12 (.value(mostrador2_2_uss));  // open: dp
  Hex_Digit_Display hex_digit_display_13 (.value(\seleção_1_placar_a ));  // open: dp
  Hex_Digit_Display hex_digit_display_14 (.value(\seleção_1_placar_b ));  // open: dp
  LED Configurando_2 (.in(mostrador2_2_lamp_config));
  and and_3 (and_3_out, clock_1_out, ~\seleção_1_a_jogando , and_1_out);  // AND_Gate

  assign Preset = Clear;

  // Notes on the sheet:
  //   Placar de A
  //   Placar de B
endmodule

module XouY_AouB (
  input  [2:0] in_1,
  output X,
  output Y,
  output A,
  output B
);

  wire and_1_out, and_2_out, and_3_out, and_4_out, and_5_out, and_6_out, not_1_out, not_2_out, not_3_out,
       not_4_out, not_5_out, not_6_out, not_7_out;

  not not_1 (not_1_out, in_1[0]);
  not not_2 (not_2_out, in_1[1]);
  not not_3 (not_3_out, in_1[2]);
  not not_4 (not_4_out, in_1[2]);
  not not_5 (not_5_out, in_1[0]);
  not not_6 (not_6_out, in_1[1]);
  not not_7 (not_7_out, in_1[2]);
  and and_1 (and_1_out, not_1_out, not_2_out, in_1[2]);
  and and_2 (and_2_out, in_1[0], not_3_out);
  and and_3 (and_3_out, in_1[1], not_4_out);
  and and_4 (and_4_out, in_1[0], in_1[2]);
  and and_5 (and_5_out, not_5_out, not_6_out, in_1[2]);
  and and_6 (and_6_out, in_1[1], not_7_out);
  or or_1 (X, and_1_out, and_2_out);
  or or_2 (Y, and_3_out, and_4_out);
  or or_3 (A, and_5_out, and_6_out);

  assign B = in_1[0];
endmodule

module Placar (
  input  Clock,
  input  Reset,
  input  Enable,
  output [3:0] out_4
);

  wire or_1_out;
  wire [3:0] registrador_ffp_1_out_9;

  or or_1 (or_1_out, Reset, Enable);
  Registrador_FFP registrador_ffp_1 (
    .D3(out_4[3]), .D2(out_4[2]), .D1(out_4[1]), .D0(out_4[0]), .Clock(Clock), .Preset(or_1_out),
    .out_9(registrador_ffp_1_out_9));  // open: Clear, Enable
  Somador_0_15 somador_0_15_1 (
    .in_1(registrador_ffp_1_out_9), .S3(out_4[3]), .S2(out_4[2]), .S1(out_4[1]), .S0(out_4[0]));
  Hex_Digit_Display hex_digit_display_1 (.value(out_4));  // open: dp
endmodule

module Somador_0_15 (
  input  [3:0] in_1,
  output S3,
  output S2,
  output S1,
  output S0
);

  wire and_1_out, and_2_out, and_3_out, and_4_out, and_5_out, and_6_out, and_7_out, and_8_out, and_9_out,
       not_1_out, not_2_out, not_3_out, not_4_out, not_5_out, not_6_out, not_7_out, not_8_out, not_9_out;

  not not_1 (not_1_out, in_1[3]);
  not not_2 (not_2_out, in_1[2]);
  not not_3 (not_3_out, in_1[1]);
  not not_4 (not_4_out, in_1[0]);
  not not_5 (not_5_out, in_1[2]);
  not not_6 (not_6_out, in_1[1]);
  not not_7 (not_7_out, in_1[0]);
  not not_8 (not_8_out, in_1[1]);
  not not_9 (not_9_out, in_1[0]);
  not not_10 (S0, in_1[0]);
  and and_1 (and_1_out, not_1_out, in_1[2], in_1[1], in_1[0]);
  and and_2 (and_2_out, in_1[3], not_2_out);
  and and_3 (and_3_out, in_1[3], not_3_out);
  and and_4 (and_4_out, in_1[3], not_4_out);
  and and_5 (and_5_out, not_5_out, in_1[1], in_1[0]);
  and and_6 (and_6_out, in_1[2], not_6_out);
  and and_7 (and_7_out, in_1[2], not_7_out);
  and and_8 (and_8_out, not_8_out, in_1[0]);
  and and_9 (and_9_out, in_1[1], not_9_out);
  or or_1 (S3, and_1_out, and_2_out, and_3_out, and_4_out);
  or or_2 (S2, and_5_out, and_6_out, and_7_out);
  or or_3 (S1, and_8_out, and_9_out);
endmodule

module MaisEstados (
  input  S1,
  input  S2,
  input  S3,
  input  ATZ,
  input  BTZ,
  output out_6,
  output out_7,
  output out_8
);

  wire [2:0] demultiplexer_1_out0, demultiplexer_1_out1, demultiplexer_1_out2, demultiplexer_1_out3,
       n00_1_d1, n01_1_d3, n10_1_s3, n11_1_s3;

  Demultiplexer #(.select(2), .width(3)) demultiplexer_1 (
    .out0(demultiplexer_1_out0), .out1(demultiplexer_1_out1), .out2(demultiplexer_1_out2),
    .out3(demultiplexer_1_out3), .in({S3, S2, S1}), .sel({BTZ, ATZ}));  // open: en
  _00 u_00_1 (
    .S3(demultiplexer_1_out0[0]), .S2(demultiplexer_1_out0[1]), .S1(demultiplexer_1_out0[2]),
    .D3(n00_1_d1[2]), .D2(n00_1_d1[1]), .D1(n00_1_d1[0]));
  _10 u_10_1 (
    .D1(demultiplexer_1_out1[0]), .D2(demultiplexer_1_out1[1]), .D3(demultiplexer_1_out1[2]),
    .S1(n10_1_s3[2]), .S2(n10_1_s3[1]), .S3(n10_1_s3[0]));
  _01 u_01_1 (
    .S1(demultiplexer_1_out2[0]), .S2(demultiplexer_1_out2[1]), .S3(demultiplexer_1_out2[2]),
    .D1(n01_1_d3[2]), .D2(n01_1_d3[1]), .D3(n01_1_d3[0]));
  _11 u_11_1 (
    .D1(demultiplexer_1_out3[0]), .D2(demultiplexer_1_out3[1]), .D3(demultiplexer_1_out3[2]),
    .S1(n11_1_s3[2]), .S2(n11_1_s3[1]), .S3(n11_1_s3[0]));
  Multiplexer #(.select(2), .width(3)) multiplexer_1 (
    .in0(n00_1_d1), .in1(n10_1_s3), .in2(n01_1_d3), .in3(n11_1_s3), .out({out_6, out_7, out_8}),
    .sel({BTZ, ATZ}));  // open: en
endmodule

module _00 (
  input  S3,
  input  S2,
  input  S1,
  output D3,
  output D2,
  output D1
);

  wire and_1_out, and_2_out, and_3_out, and_4_out, not_1_out, not_2_out, not_3_out, not_4_out;

  not not_1 (not_1_out, S1);
  not not_2 (not_2_out, S3);
  not not_3 (not_3_out, S2);
  not not_4 (not_4_out, S1);
  not not_5 (D1, S1);
  and and_1 (and_1_out, S2, S1);
  and and_2 (and_2_out, S3, not_1_out);
  and and_3 (and_3_out, not_2_out, not_3_out, S1);
  and and_4 (and_4_out, S2, not_4_out);
  or or_1 (D3, and_1_out, and_2_out);
  or or_2 (D2, and_3_out, and_4_out);
endmodule

module _10 (
  input  D1,
  input  D2,
  input  D3,
  output S1,
  output S2,
  output S3
);

  wire not_2_out;

  not not_1 (S1, D3);
  not not_2 (not_2_out, D3);
  and and_1 (S3, D1, not_2_out);

  assign S2 = 1'b0;
endmodule

module _11 (
  input  D1,
  input  D2,
  input  D3,
  output S1,
  output S2,
  output S3
);

  not not_1 (S2, D2);
  not not_2 (S3, D2);

  assign S1 = D1;
endmodule

module _01 (
  input  S1,
  input  S2,
  input  S3,
  output D1,
  output D2,
  output D3
);

  wire and_2_out, and_3_out, and_4_out, and_5_out, not_1_out, not_2_out, not_3_out, not_4_out, not_5_out,
       not_6_out, not_7_out;

  not not_1 (not_1_out, S2);
  not not_2 (not_2_out, S3);
  not not_3 (not_3_out, S2);
  not not_4 (not_4_out, S3);
  not not_5 (not_5_out, S2);
  not not_6 (not_6_out, S1);
  not not_7 (not_7_out, S3);
  and and_1 (D1, S1, not_1_out, not_2_out);
  and and_2 (and_2_out, not_3_out, S3);
  and and_3 (and_3_out, S2, not_4_out);
  and and_4 (and_4_out, S1, not_5_out);
  and and_5 (and_5_out, not_6_out, not_7_out);
  or or_1 (D2, and_2_out, and_3_out, and_4_out);
  or or_2 (D3, and_5_out, S2);
endmodule

module Verificador_FFP (
  input  [3:0] Entrada,
  input  Clock,
  output Q
);

  wire \condição_minutos_1_s ;

  \Condição___Minutos  \condição_minutos_1  (
    .I0(Entrada[3]), .I1(Entrada[2]), .I2(Entrada[1]), .I3(Entrada[0]), .S(\condição_minutos_1_s ));
  D_Flip_Flop d_ff_1 (.clk(Clock), .D(\condição_minutos_1_s ), .Q(Q));  // open: Qn, preset, en, reset
endmodule

module Teste1 (
  input  Preset,
  input  Enable,
  input  Clear
);

  wire clock_1_out, Configurar_2_out, Configurar_out, DM_2_out, DM_out, DS_2_out, DS_out,
       mostrador2_1_lamp_config, or_1_out, or_2_out, or_3_out, or_4_out, or_5_out, UM_2_out, UM_out,
       undriven, US_2_out, US_out;
  wire [3:0] mostrador2_1_dmm, mostrador2_1_dss, mostrador2_1_mum, mostrador2_1_uss;

  Hex_Digit_Display hex_digit_display_1 (.value(mostrador2_1_mum));  // open: dp
  Hex_Digit_Display hex_digit_display_2 (.value(mostrador2_1_dmm));  // open: dp
  Mostrador2 mostrador2_1 (
    .Clear(Clear), .Enable(Enable), .Preset(Preset), .Configurar(or_5_out), .Clock(clock_1_out),
    .DM(or_1_out), .UM(or_2_out), .DS(or_3_out), .US(or_4_out), .Lamp_Config(mostrador2_1_lamp_config),
    .MUM(mostrador2_1_mum), .DMM(mostrador2_1_dmm), .DSS(mostrador2_1_dss), .USS(mostrador2_1_uss),
    .Zerou(Clear));
  Hex_Digit_Display hex_digit_display_3 (.value(mostrador2_1_dss));  // open: dp
  Hex_Digit_Display hex_digit_display_4 (.value(mostrador2_1_uss));  // open: dp
  Button DM (.out(DM_out));
  Button UM (.out(UM_out));
  Button UM_2 (.out(UM_2_out));
  Button DM_2 (.out(DM_2_out));
  or or_1 (or_1_out, UM_out, UM_2_out);
  or or_2 (or_2_out, DM_out, DM_2_out);
  Button US (.out(US_out));
  Button DS (.out(DS_out));
  Button US_2 (.out(US_2_out));
  Button DS_2 (.out(DS_2_out));
  or or_3 (or_3_out, DS_out, DS_2_out);
  or or_4 (or_4_out, US_out, US_2_out);
  LED Configurando (.in(mostrador2_1_lamp_config));
  Clock clock_1 (.out(clock_1_out));
  LED led_1 (.in(undriven));
  Button Configurar (.out(Configurar_out));
  Button Configurar_2 (.out(Configurar_2_out));
  or or_5 (or_5_out, Configurar_out, Configurar_2_out);
endmodule

module Teste2 (
  input  Preset,
  input  Enable,
  input  Clear
);

  wire clock_1_out, Configurar_2_out, Configurar_out, DM_2_out, DM_out, DS_2_out, DS_out,
       mostrador2_1_lamp_config, mostrador2_2_lamp_config, or_1_out, or_2_out, or_3_out, or_4_out, or_5_out,
       UM_2_out, UM_out, undriven, US_2_out, US_out;
  wire [3:0] mostrador2_1_dmm, mostrador2_1_dss, mostrador2_1_mum, mostrador2_1_uss, mostrador2_2_dmm,
       mostrador2_2_dss, mostrador2_2_mum, mostrador2_2_uss;

  Hex_Digit_Display hex_digit_display_1 (.value(mostrador2_1_dmm));  // open: dp
  Mostrador2 mostrador2_1 (
    .Clear(Clear), .Enable(Enable), .Preset(Clear), .Configurar(or_5_out), .Clock(clock_1_out),
    .DM(or_1_out), .UM(or_3_out), .DS(or_2_out), .US(or_4_out), .Lamp_Config(mostrador2_1_lamp_config),
    .MUM(mostrador2_1_mum), .DMM(mostrador2_1_dmm), .DSS(mostrador2_1_dss), .USS(mostrador2_1_uss),
    .Zerou(Clear));
  Hex_Digit_Display hex_digit_display_2 (.value(mostrador2_1_mum));  // open: dp
  Hex_Digit_Display hex_digit_display_3 (.value(mostrador2_1_dss));  // open: dp
  Hex_Digit_Display hex_digit_display_4 (.value(mostrador2_1_uss));  // open: dp
  Button UM (.out(UM_out));
  Button UM_2 (.out(UM_2_out));
  or or_1 (or_1_out, UM_2_out, UM_out);
  Button DS (.out(DS_out));
  Button DM (.out(DM_out));
  Button DS_2 (.out(DS_2_out));
  Button DM_2 (.out(DM_2_out));
  or or_2 (or_2_out, DS_2_out, DS_out);
  or or_3 (or_3_out, DM_2_out, DM_out);
  LED Configurando (.in(mostrador2_1_lamp_config));
  Button US (.out(US_out));
  Button US_2 (.out(US_2_out));
  or or_4 (or_4_out, US_2_out, US_out);
  Clock clock_1 (.out(clock_1_out));
  LED led_1 (.in(undriven));
  LED led_2 (.in(Clear));
  Button Configurar (.out(Configurar_out));
  Button Configurar_2 (.out(Configurar_2_out));
  or or_5 (or_5_out, Configurar_2_out, Configurar_out);
  Hex_Digit_Display hex_digit_display_5 (.value(mostrador2_2_mum));  // open: dp
  Hex_Digit_Display hex_digit_display_6 (.value(mostrador2_2_dmm));  // open: dp
  Mostrador2 mostrador2_2 (
    .Clear(Clear), .Enable(Enable), .Preset(Clear), .Configurar(or_5_out), .Clock(clock_1_out),
    .DM(or_1_out), .UM(or_3_out), .DS(or_2_out), .US(or_4_out), .Lamp_Config(mostrador2_2_lamp_config),
    .MUM(mostrador2_2_mum), .DMM(mostrador2_2_dmm), .DSS(mostrador2_2_dss), .USS(mostrador2_2_uss),
    .Zerou(Clear));
  Hex_Digit_Display hex_digit_display_7 (.value(mostrador2_2_dss));  // open: dp
  Hex_Digit_Display hex_digit_display_8 (.value(mostrador2_2_uss));  // open: dp
  LED Configurando_2 (.in(mostrador2_2_lamp_config));

  assign Preset = Clear;
endmodule

module FazAcertar (
  input  A1,
  input  A2,
  input  A3,
  output S1
);

  wire and_1_out, not_1_out, not_2_out;

  not not_1 (not_1_out, A2);
  and and_1 (and_1_out, not_1_out, not_2_out);
  not not_2 (not_2_out, A3);
  or or_1 (S1, and_1_out, A1);
endmodule
